// Logisim project ALU.circ as structural Verilog: 21 circuits, main circuit EQUAL8BIT
module main (
  input  [7:0] A,
  input  [7:0] B,
  input  [3:0] slctOP,
  output Erreur,
  output [7:0] Sortie
);

  wire [7:0] bloc_op_ari_1_out_4, bloc_op_comp_1_s, bloc_op_log_1_s, lsl_1_sortie, multiplexer_1_out,
       multiplexer_2_out;

  LSL lsl_1 (.A(A), .Sortie(lsl_1_sortie));
  BLOC_OP_ARI bloc_op_ari_1 (.A(A), .SlctOP(slctOP[1:0]), .B(B), .out_4(bloc_op_ari_1_out_4));
  BLOC_OP_LOG bloc_op_log_1 (.A(B), .SlctOP(slctOP[1:0]), .B(A), .S(bloc_op_log_1_s));
  BLOC_OP_COMP bloc_op_comp_1 (.A(B), .SlctOP(slctOP[1:0]), .B(A), .S(bloc_op_comp_1_s));
  Multiplexer #(.width(8)) multiplexer_1 (
    .in0(lsl_1_sortie), .in1(bloc_op_ari_1_out_4), .out(multiplexer_1_out), .sel(slctOP[2]));
  Multiplexer #(.width(8)) multiplexer_2 (
    .in0(bloc_op_log_1_s), .in1(bloc_op_comp_1_s), .out(multiplexer_2_out), .sel(slctOP[2]));
  Multiplexer #(.width(8)) multiplexer_3 (
    .in0(multiplexer_1_out), .in1(multiplexer_2_out), .out(Sortie), .sel(slctOP[3]));
endmodule

module EQUAL (
  input  A,
  input  B,
  output S
);

  wire and_1_out, and_2_out, not_1_out, not_2_out;

  and and_1 (and_1_out, A, B);
  not not_1 (not_1_out, A);
  and and_2 (and_2_out, not_1_out, not_2_out);
  not not_2 (not_2_out, B);
  or or_1 (S, and_1_out, and_2_out);
endmodule

module DIFF (
  input  A,
  input  B,
  output S
);

  wire and_1_out, and_2_out, not_1_out, not_2_out, or_1_out;

  and and_1 (and_1_out, A, B);
  not not_1 (not_1_out, A);
  and and_2 (and_2_out, not_1_out, not_2_out);
  not not_2 (not_2_out, B);
  or or_1 (or_1_out, and_1_out, and_2_out);
  not not_3 (S, or_1_out);
endmodule

module INF (
  input  A,
  input  B,
  output S
);

  wire not_1_out;

  not not_1 (not_1_out, A);
  and and_1 (S, not_1_out, B);
endmodule

module INF_FULL (
  input  A,
  input  B,
  input  R_1,
  output S
);

  wire and_1_out, and_2_out, and_3_out, not_1_out;

  not not_1 (not_1_out, A);
  and and_1 (and_1_out, not_1_out, R_1);
  and and_2 (and_2_out, not_1_out, B);
  and and_3 (and_3_out, B, R_1);
  or or_1 (S, and_1_out, and_2_out, and_3_out);
endmodule

module SUP (
  input  A,
  input  B,
  output S
);

  wire not_1_out;

  not not_1 (not_1_out, A);
  and and_1 (S, not_1_out, B);
endmodule

module SUP_FULL (
  input  A,
  input  B,
  input  R_1,
  output S
);

  wire and_1_out, and_2_out, and_3_out, not_1_out;

  not not_1 (not_1_out, B);
  and and_1 (and_1_out, A, R_1);
  and and_2 (and_2_out, A, not_1_out);
  and and_3 (and_3_out, not_1_out, R_1);
  or or_1 (S, and_1_out, and_2_out, and_3_out);
endmodule

module EQUAL8BIT (
  input  [7:0] A,
  input  [7:0] B,
  output out_3
);

  wire equal_1_s, equal_2_s, equal_3_s, equal_4_s, equal_5_s, equal_6_s, equal_7_s, equal_8_s;

  EQUAL equal_1 (.A(A[0]), .B(B[0]), .S(equal_1_s));
  EQUAL equal_2 (.A(A[1]), .B(B[1]), .S(equal_2_s));
  EQUAL equal_3 (.A(A[2]), .B(B[2]), .S(equal_3_s));
  EQUAL equal_4 (.A(A[3]), .B(B[3]), .S(equal_4_s));
  EQUAL equal_5 (.A(A[4]), .B(B[4]), .S(equal_5_s));
  EQUAL equal_6 (.A(A[5]), .B(B[5]), .S(equal_6_s));
  EQUAL equal_7 (.A(A[6]), .B(B[6]), .S(equal_7_s));
  EQUAL equal_8 (.A(A[7]), .B(B[7]), .S(equal_8_s));
  and and_1 (out_3, equal_1_s, equal_2_s, equal_3_s, equal_4_s, equal_5_s, equal_6_s, equal_7_s, equal_8_s);
endmodule

module DIFF8BIT (
  input  [7:0] A,
  input  [7:0] B,
  output out_3
);

  wire diff_1_s, diff_2_s, diff_3_s, diff_4_s, diff_5_s, diff_6_s, diff_7_s, diff_8_s;

  DIFF diff_1 (.A(A[0]), .B(B[0]), .S(diff_1_s));
  DIFF diff_2 (.A(A[1]), .B(B[1]), .S(diff_2_s));
  DIFF diff_3 (.A(A[2]), .B(B[2]), .S(diff_3_s));
  DIFF diff_4 (.A(A[3]), .B(B[3]), .S(diff_4_s));
  DIFF diff_5 (.A(A[4]), .B(B[4]), .S(diff_5_s));
  DIFF diff_6 (.A(A[5]), .B(B[5]), .S(diff_6_s));
  DIFF diff_7 (.A(A[6]), .B(B[6]), .S(diff_7_s));
  DIFF diff_8 (.A(A[7]), .B(B[7]), .S(diff_8_s));
  or or_1 (out_3, diff_1_s, diff_2_s, diff_3_s, diff_4_s, diff_5_s, diff_6_s, diff_7_s, diff_8_s);
endmodule

module INF8BIT (
  input  [7:0] A,
  input  [7:0] B,
  output out_3
);

  wire inf_full_1_s, inf_full_2_s, inf_full_3_s, inf_full_4_s, inf_full_5_s, inf_full_6_s, inf_full_7_s;

  INF_FULL inf_full_1 (.A(A[0]), .B(B[0]), .R_1(1'b0), .S(inf_full_1_s));
  INF_FULL inf_full_2 (.A(A[1]), .B(B[1]), .R_1(inf_full_1_s), .S(inf_full_2_s));
  INF_FULL inf_full_3 (.A(A[2]), .B(B[2]), .R_1(inf_full_2_s), .S(inf_full_3_s));
  INF_FULL inf_full_4 (.A(A[3]), .B(B[3]), .R_1(inf_full_3_s), .S(inf_full_4_s));
  INF_FULL inf_full_5 (.A(A[4]), .B(B[4]), .R_1(inf_full_4_s), .S(inf_full_5_s));
  INF_FULL inf_full_6 (.A(A[5]), .B(B[5]), .R_1(inf_full_5_s), .S(inf_full_6_s));
  INF_FULL inf_full_7 (.A(A[6]), .B(B[6]), .R_1(inf_full_6_s), .S(inf_full_7_s));
  INF_FULL inf_full_8 (.A(A[7]), .B(B[7]), .R_1(inf_full_7_s), .S(out_3));
endmodule

module SUP8BIT (
  input  [7:0] A,
  input  [7:0] B,
  output out_3
);

  wire sup_full_1_s, sup_full_2_s, sup_full_3_s, sup_full_4_s, sup_full_5_s, sup_full_6_s, sup_full_7_s;

  SUP_FULL sup_full_1 (.A(A[0]), .B(B[0]), .R_1(1'b0), .S(sup_full_1_s));
  SUP_FULL sup_full_2 (.A(A[1]), .B(B[1]), .R_1(sup_full_1_s), .S(sup_full_2_s));
  SUP_FULL sup_full_3 (.A(A[2]), .B(B[2]), .R_1(sup_full_2_s), .S(sup_full_3_s));
  SUP_FULL sup_full_4 (.A(A[3]), .B(B[3]), .R_1(sup_full_3_s), .S(sup_full_4_s));
  SUP_FULL sup_full_5 (.A(A[4]), .B(B[4]), .R_1(sup_full_4_s), .S(sup_full_5_s));
  SUP_FULL sup_full_6 (.A(A[5]), .B(B[5]), .R_1(sup_full_5_s), .S(sup_full_6_s));
  SUP_FULL sup_full_7 (.A(A[6]), .B(B[6]), .R_1(sup_full_6_s), .S(sup_full_7_s));
  SUP_FULL sup_full_8 (.A(A[7]), .B(B[7]), .R_1(sup_full_7_s), .S(out_3));
endmodule

module ET (
  input  [7:0] A,
  input  [7:0] B,
  output [7:0] out_3
);

  assign out_3 = A & B;  // AND_Gate and_1, 8 bits wide
endmodule

module OU (
  input  [7:0] A,
  input  [7:0] B,
  output [7:0] out_3
);

  assign out_3 = A | B;  // OR_Gate or_1, 8 bits wide
endmodule

module XOU (
  input  [7:0] A,
  input  [7:0] B,
  output [7:0] out_3
);

  assign out_3 = A ^ B;  // XOR_Gate xor_1, 8 bits wide
endmodule

module LSL (
  input  [7:0] A,
  output [7:0] Sortie
);


  assign Sortie = {A[6:0], 1'b0};
  // also tied to GND on the sheet: A[7]
endmodule

module BLOC_OP_LOG (
  input  [7:0] A,
  input  [1:0] SlctOP,
  input  [7:0] B,
  output [7:0] S
);

  wire [7:0] et_1_out_3, multiplexer_1_out, ou_1_out_3, xou_1_out_3;

  ET et_1 (.A(A), .B(B), .out_3(et_1_out_3));
  OU ou_1 (.A(A), .B(B), .out_3(ou_1_out_3));
  XOU xou_1 (.A(A), .B(B), .out_3(xou_1_out_3));
  Multiplexer #(.width(8)) multiplexer_1 (
    .in0(ou_1_out_3), .in1(xou_1_out_3), .out(multiplexer_1_out), .sel(SlctOP[1]));
  Multiplexer #(.width(8)) multiplexer_2 (.in0(et_1_out_3), .in1(multiplexer_1_out), .out(S), .sel(SlctOP[0]));
endmodule

module BLOC_OP_COMP (
  input  [7:0] A,
  input  [1:0] SlctOP,
  input  [7:0] B,
  output [7:0] S
);

  wire diff8bit_1_out_3, equal8bit_1_out_3, inf8bit_1_out_3, multiplexer_1_out, multiplexer_2_out,
       sup8bit_1_out_3;

  EQUAL8BIT equal8bit_1 (.A(A), .B(B), .out_3(equal8bit_1_out_3));
  DIFF8BIT diff8bit_1 (.A(A), .B(B), .out_3(diff8bit_1_out_3));
  INF8BIT inf8bit_1 (.A(A), .B(B), .out_3(inf8bit_1_out_3));
  SUP8BIT sup8bit_1 (.A(A), .B(B), .out_3(sup8bit_1_out_3));
  Multiplexer multiplexer_1 (.in0(equal8bit_1_out_3), .in1(diff8bit_1_out_3), .out(multiplexer_1_out), .sel(SlctOP[1]));
  Multiplexer multiplexer_2 (.in0(inf8bit_1_out_3), .in1(sup8bit_1_out_3), .out(multiplexer_2_out), .sel(SlctOP[1]));
  Multiplexer multiplexer_3 (.in0(multiplexer_1_out), .in1(multiplexer_2_out), .out(S[0]), .sel(SlctOP[0]));

  assign S[7:1] = {7{1'b0}};
endmodule

module BLOC_OP_ARI (
  input  [7:0] A,
  input  [1:0] SlctOP,
  input  [7:0] B,
  output [7:0] out_4
);

  wire [7:0] add_1_s, sub_1_r;

  ADD add_1 (.A(A), .B(B), .S(add_1_s));
  SUB sub_1 (.B(B), .A(A), .R(sub_1_r));
  Multiplexer #(.width(8)) multiplexer_1 (.in0(add_1_s), .in1(sub_1_r), .out(out_4), .sel(SlctOP[1]));
endmodule

module add1bit (
  input  Re,
  input  A,
  input  B,
  output S,
  output Rs
);

  wire and_1_out, and_2_out, or_1_out, xor_1_out;

  xor xor_1 (xor_1_out, A, B);
  or or_1 (or_1_out, B, Re);
  xor xor_2 (S, xor_1_out, Re);
  and and_1 (and_1_out, or_1_out, A);
  or or_2 (Rs, and_1_out, and_2_out);
  and and_2 (and_2_out, B, Re);
endmodule

module ADD (
  input  [7:0] A,
  input  [7:0] B,
  output [7:0] S
);

  wire add1bit_1_rs, add1bit_2_rs, add1bit_3_rs, add1bit_4_rs, add1bit_5_rs, add1bit_6_rs, add1bit_7_rs;

  add1bit add1bit_1 (.A(A[0]), .B(B[0]), .S(S[0]), .Rs(add1bit_1_rs));  // open: Re
  add1bit add1bit_2 (.Re(add1bit_1_rs), .A(A[1]), .B(B[1]), .S(S[1]), .Rs(add1bit_2_rs));
  add1bit add1bit_3 (.Re(add1bit_2_rs), .A(A[2]), .B(B[2]), .S(S[2]), .Rs(add1bit_3_rs));
  add1bit add1bit_4 (.Re(add1bit_3_rs), .A(A[3]), .B(B[3]), .S(S[3]), .Rs(add1bit_4_rs));
  add1bit add1bit_5 (.Re(add1bit_4_rs), .A(A[4]), .B(B[4]), .S(S[4]), .Rs(add1bit_5_rs));
  add1bit add1bit_6 (.Re(add1bit_5_rs), .A(A[5]), .B(B[5]), .S(S[5]), .Rs(add1bit_6_rs));
  add1bit add1bit_7 (.Re(add1bit_6_rs), .A(A[6]), .B(B[6]), .S(S[6]), .Rs(add1bit_7_rs));
  add1bit add1bit_8 (.Re(add1bit_7_rs), .A(A[7]), .B(B[7]), .S(S[7]));  // open: Rs
endmodule

module SUB (
  input  [7:0] B,
  input  [7:0] A,
  output [7:0] R
);

  wire [7:0] add_1_s, not_1_out;

  assign not_1_out = ~B;  // NOT_Gate not_1, 8 bits wide
  ADD add_1 (.A(not_1_out), .B(8'h1), .S(add_1_s));
  ADD add_2 (.A(add_1_s), .B(A), .S(R));
endmodule
