// Logisim project Processeur .circ as structural Verilog: 38 circuits, main circuit Equal_8Bit
module main (
  input  CLK,
  output [7:0] S,
  output Er
);

  wire decodeur_1_p3, decodeur_1_p4, decodeur_1_p5, decodeur_1_p6, decodeur_1_p7, decodeur_1_p8;
  wire [1:0] decodeur_1_p9;
  wire [7:0] Donnees_dout, multiplexer_1_out, reg_alu_1_p9, regip_1_s, undriven;
  wire [23:0] Instruction_dout, RegIF_q;

  RegIP regip_1 (.CLK(CLK), .S(regip_1_s));  // open: Adresse, JUMP_EN
  RAM #(.dataWidth(24)) Instruction (.addr(regip_1_s), .oe(1'b1), .clk(CLK), .dout(Instruction_dout));  // open: we, din
  Register #(.width(24)) RegIF (.D(Instruction_dout), .en(1'b1), .clk(CLK), .Q(RegIF_q));  // open: clr
  RAM Donnees (.din(reg_alu_1_p9), .dout(Donnees_dout));  // open: addr, we, oe, clk
  // decodeur decodeur_1: pin names not known; wires that end beside it: CLK, RegIF_q, decodeur_1_p3, decodeur_1_p4, decodeur_1_p5, decodeur_1_p6, decodeur_1_p7, decodeur_1_p8, decodeur_1_p9
  Multiplexer #(.select(2), .width(8)) multiplexer_1 (
    .in0(S), .in1(Donnees_dout), .in2(undriven), .out(multiplexer_1_out), .sel(decodeur_1_p9));  // open: in3
  // Reg_ALU reg_alu_1: pin names not known; wires that end beside it: CLK, multiplexer_1_out, decodeur_1_p6, decodeur_1_p8, decodeur_1_p3, decodeur_1_p5, decodeur_1_p4, decodeur_1_p7, reg_alu_1_p9, S, Er
endmodule

module decodeur (
  input  CLK,
  input  [23:0] in_2,
  output [7:0] ADDR8,
  output [7:0] JUMP,
  output WE,
  output [1:0] SlctType,
  output [2:0] SlctOP,
  output out_8,
  output [3:0] RIn1,
  output [3:0] RIn2,
  output [7:0] CNST,
  output [3:0] Rout
);

  wire decidmemoire_1_cnst;
  wire [23:4] reg_24bit_1_q;

  Reg_24Bit reg_24bit_1 (
    .CLK(CLK), .WE(1'b1), .D(in_2),
    .Q({reg_24bit_1_q[23:21], SlctOP, SlctType, RIn1, RIn2, reg_24bit_1_q[7:4], Rout}));
  Deco_WE deco_we_1 (.in_1({reg_24bit_1_q[23:21], SlctOP, SlctType}), .WE(WE));
  DecidMemoire decidmemoire_1 (
    .E({reg_24bit_1_q[21], SlctOP, SlctType}), .Stor(out_8), .Cnst(decidmemoire_1_cnst));  // open: S, Load
  Multiplexer #(.width(8)) multiplexer_1 (
    .in1({reg_24bit_1_q[7:4], RIn2}), .out(CNST), .sel(decidmemoire_1_cnst));  // open: in0
endmodule

module Deco_WE (
  input  [7:0] in_1,
  output WE
);

  wire equal_8bit_1_s, equal_8bit_2_s, equal_8bit_3_s, equal_8bit_4_s, equal_8bit_5_s, equal_8bit_6_s,
       equal_8bit_7_s, equal_8bit_8_s, equal_8bit_9_s, equal_8bit_10_s, equal_8bit_11_s, equal_8bit_12_s,
       equal_8bit_13_s;

  Equal_8Bit equal_8bit_1 (.A(in_1), .B(8'h18), .S(equal_8bit_1_s));
  Equal_8Bit equal_8bit_2 (.A(in_1), .B(8'h19), .S(equal_8bit_2_s));
  Equal_8Bit equal_8bit_3 (.A(in_1), .B(8'h10), .S(equal_8bit_3_s));
  Equal_8Bit equal_8bit_4 (.A(in_1), .B(8'h11), .S(equal_8bit_4_s));
  Equal_8Bit equal_8bit_5 (.A(in_1), .B(8'h12), .S(equal_8bit_5_s));
  Equal_8Bit equal_8bit_6 (.A(in_1), .B(8'h9), .S(equal_8bit_6_s));
  Equal_8Bit equal_8bit_7 (.A(in_1), .B(8'ha), .S(equal_8bit_7_s));
  Equal_8Bit equal_8bit_8 (.A(in_1), .B(8'hb), .S(equal_8bit_8_s));
  Equal_8Bit equal_8bit_9 (.A(in_1), .B(8'hc), .S(equal_8bit_9_s));
  Equal_8Bit equal_8bit_10 (.A(in_1), .B(8'h1), .S(equal_8bit_10_s));
  Equal_8Bit equal_8bit_11 (.A(in_1), .B(8'h3), .S(equal_8bit_11_s));
  Equal_8Bit equal_8bit_12 (.A(in_1), .B(8'h5), .S(equal_8bit_12_s));
  Equal_8Bit equal_8bit_13 (.A(in_1), .B(8'h6), .S(equal_8bit_13_s));
  or or_1 (WE, equal_8bit_1_s, equal_8bit_2_s, equal_8bit_3_s, equal_8bit_4_s, equal_8bit_5_s, equal_8bit_6_s, equal_8bit_7_s, equal_8bit_8_s, equal_8bit_9_s, equal_8bit_10_s, equal_8bit_11_s, equal_8bit_12_s, equal_8bit_13_s);
endmodule

module DecidMemoire (
  input  [5:0] E,
  output S,
  output Load,
  output Stor,
  output Cnst
);

  wire and_1_out, not_1_out;

  not not_1 (not_1_out, E[4]);
  Decoder #(.select(3)) decoder_1 (
    .out0(S), .out1(Load), .out2(Stor), .out3(S), .out4(Cnst), .out5(S), .out6(S), .out7(S), .sel(E[2:0]),
    .en(and_1_out));
  and and_1 (and_1_out, not_1_out, E[5]);
endmodule

module Reg_ALU (
  input  CLK,
  input  [7:0] RegIn,
  input  [3:0] SlctA,
  input  [3:0] SlctC,
  input  WE,
  input  [1:0] SlctType,
  input  [2:0] SlctOP,
  input  [3:0] SlctB,
  output [7:0] RegOut,
  output Er
);

  wire [3:0] multiplexer_1_out, multiplexer_1_out_2, multiplexer_2_out, multiplexer_2_out_2;
  wire [7:0] alu_1_s, bancreg_1_r1, bancreg_1_r2, bancreg_1_r3, bancreg_1_r4, bancreg_1_r5, bancreg_1_r6,
       bancreg_1_r7, bancreg_1_r8, bancreg_1_r9, bancreg_1_r10, bancreg_1_r11, bancreg_1_r12, bancreg_1_r13,
       bancreg_1_r14, bancreg_1_r15, bancreg_1_r16;

  BancReg bancreg_1 (
    .CLK(CLK), .C(RegIn), .SlctC(SlctC), .WE(WE), .R1(bancreg_1_r1), .R2(bancreg_1_r2), .R3(bancreg_1_r3),
    .R4(bancreg_1_r4), .R5(bancreg_1_r5), .R6(bancreg_1_r6), .R7(bancreg_1_r7), .R8(bancreg_1_r8),
    .R9(bancreg_1_r9), .R10(bancreg_1_r10), .R11(bancreg_1_r11), .R12(bancreg_1_r12), .R13(bancreg_1_r13),
    .R14(bancreg_1_r14), .R15(bancreg_1_r15), .R16(bancreg_1_r16));  // open: FLAG
  Hex_Digit_Display hex_digit_display_1 (.value(multiplexer_1_out_2));  // open: dp
  Multiplexer #(.select(4), .width(8)) multiplexer_1 (
    .in0(bancreg_1_r1), .in1(bancreg_1_r2), .in2(bancreg_1_r3), .in3(bancreg_1_r4), .in4(bancreg_1_r5),
    .in5(bancreg_1_r6), .in6(bancreg_1_r7), .in7(bancreg_1_r8), .in8(bancreg_1_r9), .in9(bancreg_1_r10),
    .in10(bancreg_1_r11), .in11(bancreg_1_r12), .in12(bancreg_1_r13), .in13(bancreg_1_r14),
    .in14(bancreg_1_r15), .in15(bancreg_1_r16), .out({multiplexer_1_out_2, multiplexer_1_out}), .sel(SlctA));
  Multiplexer #(.select(4), .width(8)) multiplexer_2 (
    .in0(bancreg_1_r1), .in1(bancreg_1_r2), .in2(bancreg_1_r3), .in3(bancreg_1_r4), .in4(bancreg_1_r5),
    .in5(bancreg_1_r6), .in6(bancreg_1_r7), .in7(bancreg_1_r8), .in8(bancreg_1_r9), .in9(bancreg_1_r10),
    .in10(bancreg_1_r11), .in11(bancreg_1_r12), .in12(bancreg_1_r13), .in13(bancreg_1_r14),
    .in14(bancreg_1_r15), .in15(bancreg_1_r16), .out({multiplexer_2_out_2, multiplexer_2_out}), .sel(SlctB));
  Hex_Digit_Display hex_digit_display_2 (.value(multiplexer_2_out_2));  // open: dp
  Hex_Digit_Display hex_digit_display_3 (.value(multiplexer_1_out));  // open: dp
  Hex_Digit_Display hex_digit_display_4 (.value(multiplexer_2_out));  // open: dp
  ALU alu_1 (
    .A({multiplexer_1_out_2, multiplexer_1_out}), .B({multiplexer_2_out_2, multiplexer_2_out}),
    .slctOP(SlctOP), .Typ(SlctType), .S(alu_1_s), .Er(Er));
  assign RegOut = alu_1_s & {8{WE}};  // AND_Gate and_1, 8 bits wide
endmodule

module ALU (
  input  [7:0] A,
  input  [7:0] B,
  input  [2:0] slctOP,
  input  [1:0] Typ,
  output [7:0] S,
  output Er
);

  wire bloc_op_ari_1_err;
  wire [7:0] bloc_op_ari_1_s, bloc_op_comp_1_s, bloc_op_log_1_s, bloc_op_rot_1_s;

  BLOC_OP_COMP bloc_op_comp_1 (.A(A), .SlctOP(slctOP), .B(B), .S(bloc_op_comp_1_s));
  BLOC_OP_ROT bloc_op_rot_1 (.A(A), .SlctOP(slctOP), .S(bloc_op_rot_1_s));
  BLOC_OP_LOG bloc_op_log_1 (.SlctOP(slctOP), .A(A), .B(B), .S(bloc_op_log_1_s));
  BLOC_OP_ARI bloc_op_ari_1 (.A(A), .SlctOP(slctOP), .B(B), .S(bloc_op_ari_1_s), .Err(bloc_op_ari_1_err));
  Multiplexer #(.select(2), .width(8)) multiplexer_1 (
    .in0(bloc_op_comp_1_s), .in1(bloc_op_rot_1_s), .in2(bloc_op_log_1_s), .in3(bloc_op_ari_1_s), .out(S),
    .sel(Typ));
  Multiplexer #(.select(2)) multiplexer_2 (
    .in0(1'b0), .in1(1'b0), .in2(1'b0), .in3(bloc_op_ari_1_err), .out(Er), .sel(Typ));
endmodule

module BancReg (
  input  CLK,
  input  [7:0] C,
  input  [3:0] SlctC,
  input  WE,
  output [7:0] R1,
  output [7:0] R2,
  output [7:0] R3,
  output [7:0] R4,
  output [7:0] R5,
  output [7:0] R6,
  output [7:0] R7,
  output [7:0] R8,
  output [7:0] R9,
  output [7:0] R10,
  output [7:0] R11,
  output [7:0] R12,
  output [7:0] R13,
  output [7:0] R14,
  output [7:0] R15,
  output [7:0] R16,
  output FLAG
);

  wire decoder_1_out0, decoder_1_out1, decoder_1_out2, decoder_1_out3, decoder_1_out4, decoder_1_out5,
       decoder_1_out6, decoder_1_out7, decoder_1_out8, decoder_1_out9, decoder_1_out10, decoder_1_out11,
       decoder_1_out12, decoder_1_out13, decoder_1_out14, decoder_1_out15;

  Decoder #(.select(4)) decoder_1 (
    .out0(decoder_1_out0), .out1(decoder_1_out1), .out2(decoder_1_out2), .out3(decoder_1_out3),
    .out4(decoder_1_out4), .out5(decoder_1_out5), .out6(decoder_1_out6), .out7(decoder_1_out7),
    .out8(decoder_1_out8), .out9(decoder_1_out9), .out10(decoder_1_out10), .out11(decoder_1_out11),
    .out12(decoder_1_out12), .out13(decoder_1_out13), .out14(decoder_1_out14), .out15(decoder_1_out15),
    .sel(SlctC), .en(WE));
  // NoConnect on C[7:1]
  Reg_8Bit reg_8bit_1 (.D(C), .WE(decoder_1_out0), .CLK(CLK), .Q(R1));
  Reg_8Bit reg_8bit_2 (.D(C), .WE(decoder_1_out1), .CLK(CLK), .Q(R2));
  Reg_8Bit reg_8bit_3 (.D(C), .WE(decoder_1_out2), .CLK(CLK), .Q(R3));
  Reg_8Bit reg_8bit_4 (.D(C), .WE(decoder_1_out3), .CLK(CLK), .Q(R4));
  Reg_8Bit reg_8bit_5 (.D(C), .WE(decoder_1_out4), .CLK(CLK), .Q(R5));
  Reg_8Bit reg_8bit_6 (.D(C), .WE(decoder_1_out5), .CLK(CLK), .Q(R6));
  Reg_8Bit reg_8bit_7 (.D(C), .WE(decoder_1_out6), .CLK(CLK), .Q(R7));
  Reg_8Bit reg_8bit_8 (.D(C), .WE(decoder_1_out7), .CLK(CLK), .Q(R8));
  Reg_8Bit reg_8bit_9 (.D(C), .WE(decoder_1_out8), .CLK(CLK), .Q(R9));
  Reg_8Bit reg_8bit_10 (.D(C), .WE(decoder_1_out9), .CLK(CLK), .Q(R10));
  Reg_8Bit reg_8bit_11 (.D(C), .WE(decoder_1_out10), .CLK(CLK), .Q(R11));
  Reg_8Bit reg_8bit_12 (.D(C), .WE(decoder_1_out11), .CLK(CLK), .Q(R12));
  Reg_8Bit reg_8bit_13 (.D(C), .WE(decoder_1_out12), .CLK(CLK), .Q(R13));
  Reg_8Bit reg_8bit_14 (.D(C), .WE(decoder_1_out13), .CLK(CLK), .Q(R14));
  Reg_8Bit reg_8bit_15 (.D(C), .WE(decoder_1_out14), .CLK(CLK), .Q(R15));
  Reg_1Bit reg_1bit_1 (.D(C[0]), .WE(decoder_1_out15), .CLK(CLK), .Q(FLAG));

  assign R16 = {{7{1'b0}}, FLAG};
endmodule

module Reg_24Bit (
  input  CLK,
  input  WE,
  input  [23:0] D,
  output [23:0] Q
);

  Reg_8Bit reg_8bit_1 (.D(D[7:0]), .WE(WE), .CLK(CLK), .Q(Q[7:0]));
  Reg_8Bit reg_8bit_2 (.D(D[15:8]), .WE(WE), .CLK(CLK), .Q(Q[15:8]));
  Reg_8Bit reg_8bit_3 (.D(D[23:16]), .WE(WE), .CLK(CLK), .Q(Q[23:16]));
endmodule

module Reg_8Bit (
  input  [7:0] D,
  input  WE,
  input  CLK,
  output [7:0] Q
);

  wire and_1_out;

  and and_1 (and_1_out, WE, CLK);
  D_Flip_Flop d_ff_1 (.D(D[0]), .clk(and_1_out), .Q(Q[0]));  // open: Qn, preset, reset
  D_Flip_Flop d_ff_2 (.D(D[1]), .clk(and_1_out), .Q(Q[1]));  // open: Qn, preset, reset
  D_Flip_Flop d_ff_3 (.D(D[2]), .clk(and_1_out), .Q(Q[2]));  // open: Qn, preset, reset
  D_Flip_Flop d_ff_4 (.D(D[3]), .clk(and_1_out), .Q(Q[3]));  // open: Qn, preset, reset
  D_Flip_Flop d_ff_5 (.D(D[4]), .clk(and_1_out), .Q(Q[4]));  // open: Qn, preset, reset
  D_Flip_Flop d_ff_6 (.D(D[5]), .clk(and_1_out), .Q(Q[5]));  // open: Qn, preset, reset
  D_Flip_Flop d_ff_7 (.D(D[6]), .clk(and_1_out), .Q(Q[6]));  // open: Qn, preset, reset
  D_Flip_Flop d_ff_8 (.D(D[7]), .clk(and_1_out), .Q(Q[7]));  // open: Qn, preset, reset
endmodule

module Reg_1Bit (
  input  D,
  input  WE,
  input  CLK,
  output Q
);

  wire and_1_out;

  and and_1 (and_1_out, WE, CLK);
  D_Flip_Flop d_ff_1 (.D(D), .clk(and_1_out), .Q(Q));  // open: Qn, preset, reset
endmodule

module BLOC_OP_LOG (
  input  [2:0] SlctOP,
  input  [7:0] A,
  input  [7:0] B,
  output [7:0] S
);

  wire [7:0] and_8bit_1_s, or_8bit_1_s, xor_8bit_1_s;

  And_8Bit and_8bit_1 (.A(A), .B(B), .S(and_8bit_1_s));
  Or_8Bit or_8bit_1 (.A(A), .B(B), .S(or_8bit_1_s));
  Xor_8Bit xor_8bit_1 (.A(A), .B(B), .S(xor_8bit_1_s));
  Multiplexer #(.select(3), .width(8)) multiplexer_1 (
    .in0(and_8bit_1_s), .in1(or_8bit_1_s), .in2(xor_8bit_1_s), .in3({8{1'b0}}), .in4({8{1'b0}}),
    .in5({8{1'b0}}), .in6({8{1'b0}}), .in7({8{1'b0}}), .out(S), .sel(SlctOP));
endmodule

module BLOC_OP_COMP (
  input  [7:0] A,
  input  [2:0] SlctOP,
  input  [7:0] B,
  output [7:0] S
);

  wire diff_8bit_1_s, equal_8bit_1_s, inf_8bit_1_s, sup_8bit_1_s;

  Equal_8Bit equal_8bit_1 (.A(A), .B(B), .S(equal_8bit_1_s));
  Diff_8Bit diff_8bit_1 (.A(A), .B(B), .S(diff_8bit_1_s));
  Inf_8Bit inf_8bit_1 (.A(A), .B(B), .S(inf_8bit_1_s));
  Sup_8Bit sup_8bit_1 (.A(A), .B(B), .S(sup_8bit_1_s));
  Multiplexer #(.select(3)) multiplexer_1 (
    .in0(1'b0), .in1(inf_8bit_1_s), .in2(1'b0), .in3(equal_8bit_1_s), .in4(1'b0), .in5(sup_8bit_1_s),
    .in6(diff_8bit_1_s), .in7(1'b0), .out(S[0]), .sel(SlctOP));

  assign S[7:1] = {7{1'b0}};
endmodule

module BLOC_OP_ARI (
  input  [7:0] A,
  input  [2:0] SlctOP,
  input  [7:0] B,
  output [7:0] S,
  output Err
);

  wire add_8bit_1_er, sub_8bit_1_er;
  wire [7:0] add_8bit_1_s, sub_8bit_1_s;

  Add_8Bit add_8bit_1 (.A(A), .B(B), .S(add_8bit_1_s), .Er(add_8bit_1_er));
  Sub_8Bit sub_8bit_1 (.A(A), .B(B), .S(sub_8bit_1_s), .Er(sub_8bit_1_er));
  or or_1 (Err, add_8bit_1_er, sub_8bit_1_er);
  Multiplexer #(.select(3), .width(8)) multiplexer_1 (
    .in0(add_8bit_1_s), .in1(sub_8bit_1_s), .in2({8{1'b0}}), .in3({8{1'b0}}), .in4({8{1'b0}}),
    .in5({8{1'b0}}), .in6({8{1'b0}}), .in7({8{1'b0}}), .out(S), .sel(SlctOP));
endmodule

module BLOC_OP_ROT (
  input  [7:0] A,
  input  [2:0] SlctOP,
  output [7:0] S
);

  wire [7:0] asr_8bit_1_s, lsl_8bit_1_s, lsr_8bit_1_s, rol_8bit_1_s, ror_8bit_1_s;

  Lsl_8Bit lsl_8bit_1 (.A(A), .S(lsl_8bit_1_s));
  Lsr_8Bit lsr_8bit_1 (.A(A), .S(lsr_8bit_1_s));
  Asr_8Bit asr_8bit_1 (.A(A), .S(asr_8bit_1_s));
  Rol_8Bit rol_8bit_1 (.A(A), .S(rol_8bit_1_s));
  Ror_8Bit ror_8bit_1 (.A(A), .S(ror_8bit_1_s));
  Multiplexer #(.select(3), .width(8)) multiplexer_1 (
    .in0({8{1'b0}}), .in1(lsl_8bit_1_s), .in2(lsr_8bit_1_s), .in3(asr_8bit_1_s), .in4(rol_8bit_1_s),
    .in5(ror_8bit_1_s), .in6({8{1'b0}}), .in7({8{1'b0}}), .out(S), .sel(SlctOP));
endmodule

module Equal_1Bit (
  input  A,
  input  B,
  output S
);

  wire and_1_out, and_2_out, not_1_out, not_2_out;

  and and_1 (and_1_out, A, B);
  not not_1 (not_1_out, A);
  and and_2 (and_2_out, not_1_out, not_2_out);
  not not_2 (not_2_out, B);
  or or_1 (S, and_1_out, and_2_out);
endmodule

module Diff_1Bit (
  input  A,
  input  B,
  output S
);

  wire and_1_out, and_2_out, not_1_out, not_2_out, or_1_out;

  and and_1 (and_1_out, A, B);
  not not_1 (not_1_out, A);
  and and_2 (and_2_out, not_1_out, not_2_out);
  not not_2 (not_2_out, B);
  or or_1 (or_1_out, and_1_out, and_2_out);
  not not_3 (S, or_1_out);
endmodule

module Inf_1Bit (
  input  A,
  input  B,
  output S
);

  wire not_1_out;

  not not_1 (not_1_out, A);
  and and_1 (S, not_1_out, B);
endmodule

module InfFull_1Bit (
  input  A,
  input  B,
  input  R_1,
  output S
);

  wire and_1_out, and_2_out, and_3_out, not_1_out;

  not not_1 (not_1_out, A);
  and and_1 (and_1_out, not_1_out, R_1);
  and and_2 (and_2_out, not_1_out, B);
  and and_3 (and_3_out, B, R_1);
  or or_1 (S, and_1_out, and_2_out, and_3_out);
endmodule

module Sup_1Bit (
  input  A,
  input  B,
  output S
);

  wire not_1_out;

  not not_1 (not_1_out, A);
  and and_1 (S, not_1_out, B);
endmodule

module SupFull_1Bit (
  input  A,
  input  B,
  input  R_1,
  output S
);

  wire and_1_out, and_2_out, and_3_out, not_1_out;

  not not_1 (not_1_out, B);
  and and_1 (and_1_out, A, R_1);
  and and_2 (and_2_out, A, not_1_out);
  and and_3 (and_3_out, not_1_out, R_1);
  or or_1 (S, and_1_out, and_2_out, and_3_out);
endmodule

module Equal_8Bit (
  input  [7:0] A,
  input  [7:0] B,
  output S
);

  wire equal_1bit_1_s, equal_1bit_2_s, equal_1bit_3_s, equal_1bit_4_s, equal_1bit_5_s, equal_1bit_6_s,
       equal_1bit_7_s, equal_1bit_8_s;

  Equal_1Bit equal_1bit_1 (.A(A[0]), .B(B[0]), .S(equal_1bit_1_s));
  Equal_1Bit equal_1bit_2 (.A(A[1]), .B(B[1]), .S(equal_1bit_2_s));
  Equal_1Bit equal_1bit_3 (.A(A[2]), .B(B[2]), .S(equal_1bit_3_s));
  Equal_1Bit equal_1bit_4 (.A(A[3]), .B(B[3]), .S(equal_1bit_4_s));
  Equal_1Bit equal_1bit_5 (.A(A[4]), .B(B[4]), .S(equal_1bit_5_s));
  Equal_1Bit equal_1bit_6 (.A(A[5]), .B(B[5]), .S(equal_1bit_6_s));
  Equal_1Bit equal_1bit_7 (.A(A[6]), .B(B[6]), .S(equal_1bit_7_s));
  Equal_1Bit equal_1bit_8 (.A(A[7]), .B(B[7]), .S(equal_1bit_8_s));
  and and_1 (S, equal_1bit_1_s, equal_1bit_2_s, equal_1bit_3_s, equal_1bit_4_s, equal_1bit_5_s, equal_1bit_6_s, equal_1bit_7_s, equal_1bit_8_s);
endmodule

module Diff_8Bit (
  input  [7:0] A,
  input  [7:0] B,
  output S
);

  wire diff_1bit_1_s, diff_1bit_2_s, diff_1bit_3_s, diff_1bit_4_s, diff_1bit_5_s, diff_1bit_6_s,
       diff_1bit_7_s, diff_1bit_8_s;

  Diff_1Bit diff_1bit_1 (.A(A[0]), .B(B[0]), .S(diff_1bit_1_s));
  Diff_1Bit diff_1bit_2 (.A(A[1]), .B(B[1]), .S(diff_1bit_2_s));
  Diff_1Bit diff_1bit_3 (.A(A[2]), .B(B[2]), .S(diff_1bit_3_s));
  Diff_1Bit diff_1bit_4 (.A(A[3]), .B(B[3]), .S(diff_1bit_4_s));
  Diff_1Bit diff_1bit_5 (.A(A[4]), .B(B[4]), .S(diff_1bit_5_s));
  Diff_1Bit diff_1bit_6 (.A(A[5]), .B(B[5]), .S(diff_1bit_6_s));
  Diff_1Bit diff_1bit_7 (.A(A[6]), .B(B[6]), .S(diff_1bit_7_s));
  Diff_1Bit diff_1bit_8 (.A(A[7]), .B(B[7]), .S(diff_1bit_8_s));
  or or_1 (S, diff_1bit_1_s, diff_1bit_2_s, diff_1bit_3_s, diff_1bit_4_s, diff_1bit_5_s, diff_1bit_6_s, diff_1bit_7_s, diff_1bit_8_s);
endmodule

module Inf_8Bit (
  input  [7:0] A,
  input  [7:0] B,
  output S
);

  wire inffull_1bit_1_s, inffull_1bit_2_s, inffull_1bit_3_s, inffull_1bit_4_s, inffull_1bit_5_s,
       inffull_1bit_6_s, inffull_1bit_7_s;

  InfFull_1Bit inffull_1bit_1 (.A(A[0]), .B(B[0]), .R_1(1'b0), .S(inffull_1bit_1_s));
  InfFull_1Bit inffull_1bit_2 (.A(A[1]), .B(B[1]), .R_1(inffull_1bit_1_s), .S(inffull_1bit_2_s));
  InfFull_1Bit inffull_1bit_3 (.A(A[2]), .B(B[2]), .R_1(inffull_1bit_2_s), .S(inffull_1bit_3_s));
  InfFull_1Bit inffull_1bit_4 (.A(A[3]), .B(B[3]), .R_1(inffull_1bit_3_s), .S(inffull_1bit_4_s));
  InfFull_1Bit inffull_1bit_5 (.A(A[4]), .B(B[4]), .R_1(inffull_1bit_4_s), .S(inffull_1bit_5_s));
  InfFull_1Bit inffull_1bit_6 (.A(A[5]), .B(B[5]), .R_1(inffull_1bit_5_s), .S(inffull_1bit_6_s));
  InfFull_1Bit inffull_1bit_7 (.A(A[6]), .B(B[6]), .R_1(inffull_1bit_6_s), .S(inffull_1bit_7_s));
  InfFull_1Bit inffull_1bit_8 (.A(A[7]), .B(B[7]), .R_1(inffull_1bit_7_s), .S(S));
endmodule

module Sup_8Bit (
  input  [7:0] A,
  input  [7:0] B,
  output S
);

  wire supfull_1bit_1_s, supfull_1bit_2_s, supfull_1bit_3_s, supfull_1bit_4_s, supfull_1bit_5_s,
       supfull_1bit_6_s, supfull_1bit_7_s;

  SupFull_1Bit supfull_1bit_1 (.A(A[0]), .B(B[0]), .R_1(1'b0), .S(supfull_1bit_1_s));
  SupFull_1Bit supfull_1bit_2 (.A(A[1]), .B(B[1]), .R_1(supfull_1bit_1_s), .S(supfull_1bit_2_s));
  SupFull_1Bit supfull_1bit_3 (.A(A[2]), .B(B[2]), .R_1(supfull_1bit_2_s), .S(supfull_1bit_3_s));
  SupFull_1Bit supfull_1bit_4 (.A(A[3]), .B(B[3]), .R_1(supfull_1bit_3_s), .S(supfull_1bit_4_s));
  SupFull_1Bit supfull_1bit_5 (.A(A[4]), .B(B[4]), .R_1(supfull_1bit_4_s), .S(supfull_1bit_5_s));
  SupFull_1Bit supfull_1bit_6 (.A(A[5]), .B(B[5]), .R_1(supfull_1bit_5_s), .S(supfull_1bit_6_s));
  SupFull_1Bit supfull_1bit_7 (.A(A[6]), .B(B[6]), .R_1(supfull_1bit_6_s), .S(supfull_1bit_7_s));
  SupFull_1Bit supfull_1bit_8 (.A(A[7]), .B(B[7]), .R_1(supfull_1bit_7_s), .S(S));
endmodule

module And_8Bit (
  input  [7:0] A,
  input  [7:0] B,
  output [7:0] S
);

  assign S = A & B;  // AND_Gate and_1, 8 bits wide
endmodule

module Or_8Bit (
  input  [7:0] A,
  input  [7:0] B,
  output [7:0] S
);

  assign S = A | B;  // OR_Gate or_1, 8 bits wide
endmodule

module Xor_8Bit (
  input  [7:0] A,
  input  [7:0] B,
  output [7:0] S
);

  assign S = A ^ B;  // XOR_Gate xor_1, 8 bits wide
endmodule

module Lsl_8Bit (
  input  [7:0] A,
  output [7:0] S
);

  // NoConnect on A[7]

  assign S = {A[6:0], 1'b0};
endmodule

module Lsr_8Bit (
  input  [7:0] A,
  output [7:0] S
);

  // NoConnect on A[0]

  assign S = {1'b0, A[7:1]};
endmodule

module Asr_8Bit (
  input  [7:0] A,
  output [7:0] S
);

  // NoConnect on A[0]

  assign S = {{2{A[7]}}, A[6:1]};
endmodule

module Rol_8Bit (
  input  [7:0] A,
  output [7:0] S
);


  assign S = {A[6:0], A[7]};
endmodule

module Ror_8Bit (
  input  [7:0] A,
  output [7:0] S
);


  assign S = {A[0], A[7:1]};
endmodule

module Add_1Bit (
  input  Re,
  input  A,
  input  B,
  output S,
  output Rs
);

  wire and_1_out, and_2_out, or_1_out, xor_1_out;

  xor xor_1 (xor_1_out, A, B);
  or or_1 (or_1_out, B, Re);
  xor xor_2 (S, xor_1_out, Re);
  and and_1 (and_1_out, or_1_out, A);
  or or_2 (Rs, and_1_out, and_2_out);
  and and_2 (and_2_out, B, Re);
endmodule

module Add_8Bit (
  input  [7:0] A,
  input  [7:0] B,
  output [7:0] S,
  output Er
);

  wire add_1bit_1_rs, add_1bit_2_rs, add_1bit_3_rs, add_1bit_4_rs, add_1bit_5_rs, add_1bit_6_rs,
       add_1bit_7_rs;

  Add_1Bit add_1bit_1 (.Re(1'b0), .A(A[0]), .B(B[0]), .S(S[0]), .Rs(add_1bit_1_rs));
  Add_1Bit add_1bit_2 (.Re(add_1bit_1_rs), .A(A[1]), .B(B[1]), .S(S[1]), .Rs(add_1bit_2_rs));
  Add_1Bit add_1bit_3 (.Re(add_1bit_2_rs), .A(A[2]), .B(B[2]), .S(S[2]), .Rs(add_1bit_3_rs));
  Add_1Bit add_1bit_4 (.Re(add_1bit_3_rs), .A(A[3]), .B(B[3]), .S(S[3]), .Rs(add_1bit_4_rs));
  Add_1Bit add_1bit_5 (.Re(add_1bit_4_rs), .A(A[4]), .B(B[4]), .S(S[4]), .Rs(add_1bit_5_rs));
  Add_1Bit add_1bit_6 (.Re(add_1bit_5_rs), .A(A[5]), .B(B[5]), .S(S[5]), .Rs(add_1bit_6_rs));
  Add_1Bit add_1bit_7 (.Re(add_1bit_6_rs), .A(A[6]), .B(B[6]), .S(S[6]), .Rs(add_1bit_7_rs));
  Add_1Bit add_1bit_8 (.Re(add_1bit_7_rs), .A(A[7]), .B(B[7]), .S(S[7]), .Rs(Er));
endmodule

module CC2_8Bit (
  input  [7:0] A,
  output [7:0] S,
  output Er
);

  wire add_8bit_1_er;
  wire [7:0] not_1_out;

  assign not_1_out = ~A;  // NOT_Gate not_1, 8 bits wide
  Add_8Bit add_8bit_1 (.A(not_1_out), .B(8'h1), .S(S), .Er(add_8bit_1_er));
  // NoConnect on add_8bit_1_er
  Equal_8Bit equal_8bit_1 (.A(A), .B(8'h80), .S(Er));
endmodule

module Sub_8Bit (
  input  [7:0] A,
  input  [7:0] B,
  output [7:0] S,
  output Er
);

  wire add_8bit_1_er, cc2_8bit_1_er;
  wire [7:0] cc2_8bit_1_s;

  CC2_8Bit cc2_8bit_1 (.A(B), .S(cc2_8bit_1_s), .Er(cc2_8bit_1_er));
  Add_8Bit add_8bit_1 (.A(A), .B(cc2_8bit_1_s), .S(S), .Er(add_8bit_1_er));
  or or_1 (Er, add_8bit_1_er, cc2_8bit_1_er);
endmodule

module Chemin (
  input  CLK
);

  wire [7:0] regip_1_s;
  wire [23:0] Instruction_dout, RegIF_q;

  RegIP regip_1 (.CLK(CLK), .S(regip_1_s));  // open: Adresse, JUMP_EN
  RAM #(.dataWidth(24)) Instruction (.addr(regip_1_s), .oe(1'b1), .clk(CLK), .dout(Instruction_dout));  // open: we, din
  Register #(.width(24)) RegIF (.D(Instruction_dout), .en(1'b1), .clk(CLK), .Q(RegIF_q));  // open: clr
  RAM Donnees ();  // open: addr, we, oe, clk, din, dout
  decodeur decodeur_1 (
    .CLK(CLK), .in_2(RegIF_q));  // open: ADDR8, JUMP, WE, SlctType, SlctOP, out_8, RIn1, RIn2, CNST, Rout
endmodule

module RegIP (
  input  [7:0] Adresse,
  input  CLK,
  input  JUMP_EN,
  output [7:0] S
);

  wire add_8bit_1_er;
  wire [7:0] multiplexer_1_out, register_1_q;

  Multiplexer #(.width(8)) multiplexer_1 (.in0(S), .in1(Adresse), .out(multiplexer_1_out), .sel(JUMP_EN));
  Register register_1 (.D(multiplexer_1_out), .en(1'b1), .clk(CLK), .Q(register_1_q));  // open: clr
  Add_8Bit add_8bit_1 (.A(register_1_q), .B(8'h1), .S(S), .Er(add_8bit_1_er));
  // NoConnect on add_8bit_1_er
endmodule
