// Logisim project Processeur.circ as structural Verilog: 52 circuits, main circuit Processeur
module Processeur (
);

  wire clock_1_out, decodeur_1_jmp, decodeur_1_stor, decodeur_1_we, reg_alu_1_er, reg_alu_1_rcmp;
  wire [1:0] decodeur_1_slct, decodeur_1_slcttype;
  wire [2:0] decodeur_1_slctop;
  wire [3:0] addr_unit_1_regin, addr_unit_1_regin_2, affichage_8bit_1_s1, affichage_8bit_1_s2,
       affichage_8bit_2_s1, affichage_8bit_2_s2, cptrebour_1_s1, cptrebour_1_s2, decodeur_1_rin1,
       decodeur_1_rin2, decodeur_1_rout, reg_alu_1_aluout, reg_alu_1_aluout_2, reg_alu_1_print_r,
       reg_alu_1_print_r_2, reg_alu_1_regout, reg_alu_1_regout_2;
  wire [7:0] addr_unit_1_adddrdata, addr_unit_1_addrcode, addr_unit_1_print_s, decodeur_1_addr8,
       reg_alu_1_print_a, reg_alu_1_print_b, reg_alu_1_print_r_3, reg_alu_1_print_r_5, stor_unit_1_data_out;
  wire [23:0] RegIF_q, stor_unit_1_code_out;
  wire [55:16] reg_alu_1_print_r_4;

  Clock clock_1 (.out(clock_1_out));
  Hex_Digit_Display hex_digit_display_1 (.value(reg_alu_1_print_r_5[7:4]));  // open: dp
  Hex_Digit_Display hex_digit_display_2 (.value(reg_alu_1_print_r_5[3:0]));  // open: dp
  Hex_Digit_Display hex_digit_display_3 (.value(reg_alu_1_print_r_4[55:52]));  // open: dp
  Hex_Digit_Display hex_digit_display_4 (.value(reg_alu_1_print_r_4[51:48]));  // open: dp
  STOR_UNIT stor_unit_1 (
    .ADDRCode(addr_unit_1_addrcode), .ADDDRData(addr_unit_1_adddrdata),
    .DATA_IN({reg_alu_1_regout_2, reg_alu_1_regout}), .STOR(decodeur_1_stor), .CLK(clock_1_out),
    .DATA_OUT(stor_unit_1_data_out), .Code_OUT(stor_unit_1_code_out));
  Hex_Digit_Display hex_digit_display_5 (.value(reg_alu_1_print_r_4[47:44]));  // open: dp
  Hex_Digit_Display hex_digit_display_6 (.value(reg_alu_1_print_r_4[43:40]));  // open: dp
  ADDR_UNIT addr_unit_1 (
    .Slct(decodeur_1_slct), .CLK(clock_1_out), .JMP(decodeur_1_jmp), .RAM(stor_unit_1_data_out),
    .ADDR8(decodeur_1_addr8), .ALU({reg_alu_1_aluout_2, reg_alu_1_aluout}),
    .RegIn({addr_unit_1_regin_2, addr_unit_1_regin}), .ADDRCode(addr_unit_1_addrcode),
    .ADDDRData(addr_unit_1_adddrdata), .PRINT_S(addr_unit_1_print_s));
  Register #(.width(24)) RegIF (.D(stor_unit_1_code_out), .en(1'b1), .clk(clock_1_out), .Q(RegIF_q));  // open: clr
  Hex_Digit_Display hex_digit_display_7 (.value(reg_alu_1_print_r_4[39:36]));  // open: dp
  Hex_Digit_Display hex_digit_display_8 (.value(RegIF_q[23:20]));  // open: dp
  Hex_Digit_Display hex_digit_display_9 (.value(reg_alu_1_print_r_4[35:32]));  // open: dp
  Hex_Digit_Display hex_digit_display_10 (.value(RegIF_q[19:16]));  // open: dp
  Hex_Digit_Display hex_digit_display_11 (.value(reg_alu_1_print_r_4[31:28]));  // open: dp
  Hex_Digit_Display hex_digit_display_12 (.value(addr_unit_1_regin_2));  // open: dp
  Hex_Digit_Display hex_digit_display_13 (.value(addr_unit_1_regin));  // open: dp
  Hex_Digit_Display hex_digit_display_14 (.value(cptrebour_1_s1));  // open: dp
  CptRebour cptrebour_1 (.E(addr_unit_1_print_s), .S2(cptrebour_1_s2), .S1(cptrebour_1_s1));
  Hex_Digit_Display hex_digit_display_15 (.value(RegIF_q[15:12]));  // open: dp
  Hex_Digit_Display hex_digit_display_16 (.value(RegIF_q[11:8]));  // open: dp
  Hex_Digit_Display hex_digit_display_17 (.value(reg_alu_1_print_r_4[27:24]));  // open: dp
  Hex_Digit_Display hex_digit_display_18 (.value(cptrebour_1_s2));  // open: dp
  Hex_Digit_Display hex_digit_display_19 (.value(RegIF_q[7:4]));  // open: dp
  Hex_Digit_Display hex_digit_display_20 (.value(reg_alu_1_print_r_4[23:20]));  // open: dp
  Hex_Digit_Display hex_digit_display_21 (.value(RegIF_q[3:0]));  // open: dp
  decodeur decodeur_1 (
    .RCMP(reg_alu_1_rcmp), .in_3(RegIF_q), .CLK(clock_1_out), .ADDR8(decodeur_1_addr8),
    .SlctOP(decodeur_1_slctop), .SlctType(decodeur_1_slcttype), .Slct(decodeur_1_slct),
    .STOR(decodeur_1_stor), .WE(decodeur_1_we), .JMP(decodeur_1_jmp), .RIn1(decodeur_1_rin1),
    .RIn2(decodeur_1_rin2), .Rout(decodeur_1_rout));
  Hex_Digit_Display hex_digit_display_22 (.value(reg_alu_1_print_r_4[19:16]));  // open: dp
  Hex_Digit_Display hex_digit_display_23 (.value(reg_alu_1_regout));  // open: dp
  Hex_Digit_Display hex_digit_display_24 (.value(reg_alu_1_regout_2));  // open: dp
  Hex_Digit_Display hex_digit_display_25 (.value(reg_alu_1_print_r_3[7:4]));  // open: dp
  Hex_Digit_Display hex_digit_display_26 (.value(reg_alu_1_print_r_3[3:0]));  // open: dp
  Hex_Digit_Display hex_digit_display_27 (.value(reg_alu_1_aluout_2));  // open: dp
  Hex_Digit_Display hex_digit_display_28 (.value(reg_alu_1_print_r_2));  // open: dp
  Hex_Digit_Display hex_digit_display_29 (.value(reg_alu_1_print_r));  // open: dp
  Hex_Digit_Display hex_digit_display_30 (.value(reg_alu_1_aluout));  // open: dp
  Hex_Digit_Display hex_digit_display_31 (.value(affichage_8bit_1_s1));  // open: dp
  Affichage_8bit affichage_8bit_1 (
    .Eg(reg_alu_1_print_a), .S1(affichage_8bit_1_s1), .S2(affichage_8bit_1_s2));  // open: Eb, Ed
  Hex_Digit_Display hex_digit_display_32 (.value(affichage_8bit_1_s2));  // open: dp
  Hex_Digit_Display hex_digit_display_33 (.value(affichage_8bit_2_s1));  // open: dp
  Affichage_8bit affichage_8bit_2 (
    .Eg(reg_alu_1_print_b), .S1(affichage_8bit_2_s1), .S2(affichage_8bit_2_s2));  // open: Eb, Ed
  Reg_ALU reg_alu_1 (
    .SlctOP(decodeur_1_slctop), .SlctType(decodeur_1_slcttype),
    .RegIn({addr_unit_1_regin_2, addr_unit_1_regin}), .WE(decodeur_1_we), .CLK(clock_1_out),
    .SlctC(decodeur_1_rout), .SlctB(decodeur_1_rin2), .SlctA(decodeur_1_rin1),
    .RegOut({reg_alu_1_regout_2, reg_alu_1_regout}), .Er(reg_alu_1_er), .RCMP(reg_alu_1_rcmp),
    .ALUOut({reg_alu_1_aluout_2, reg_alu_1_aluout}), .PRINT_B(reg_alu_1_print_b),
    .PRINT_A(reg_alu_1_print_a),
    .PRINT_R({reg_alu_1_print_r_5, reg_alu_1_print_r_4, reg_alu_1_print_r_3, reg_alu_1_print_r_2, reg_alu_1_print_r}));
  Hex_Digit_Display hex_digit_display_34 (.value(affichage_8bit_2_s2));  // open: dp
  // Probe on reg_alu_1_er

  // Notes on the sheet:
  //   Registre 1
  //   Registre 2
  //   Registre 3
  //   Registre 4
  //   Reg In
  //   Instruction FETCH
  //   Registre 5
  //   Incrémentation Instructions
  //   Registre 6
  //   Reg Out
  //   Registre 7
  //   Registre 8 (RCMP)
  //   ALU Out
  //   Entrée A
  //   Entrée B
endmodule

module ADDR_UNIT (
  input  [7:0] RAM,
  input  [7:0] ALU,
  input  [7:0] ADDR8,
  input  [1:0] Slct,
  input  CLK,
  input  JMP,
  output [7:0] ADDDRData,
  output [7:0] RegIn,
  output [7:0] ADDRCode,
  output [7:0] PRINT_S
);

  wire [7:0] adder_1_out;

  Register register_1 (.D(ADDRCode), .en(1'b1), .clk(CLK), .Q(PRINT_S));  // open: clr
  Adder adder_1 (.a(PRINT_S), .b(8'h1), .out(adder_1_out));  // open: cin, cout
  Multiplexer #(.width(8)) multiplexer_1 (.in0(adder_1_out), .in1(ADDR8), .out(ADDRCode), .sel(JMP));
  Multiplexer #(.select(2), .width(8)) multiplexer_2 (
    .in0(ALU), .in1(RAM), .in2(ADDR8), .in3({8{1'b0}}), .out(RegIn), .sel(Slct));

  assign ADDDRData = ADDR8;
endmodule

module STOR_UNIT (
  input  CLK,
  input  [7:0] ADDDRData,
  input  STOR,
  input  [7:0] DATA_IN,
  input  [7:0] ADDRCode,
  output [7:0] DATA_OUT,
  output [23:0] Code_OUT
);

  RAM Donnees (.addr(ADDDRData), .we(STOR), .oe(1'b1), .clk(CLK), .din(DATA_IN), .dout(DATA_OUT));
  RAM #(.dataWidth(24)) Instruction (
    .addr(ADDRCode), .we(1'b0), .oe(1'b1), .clk(CLK), .din({24{1'b0}}), .dout(Code_OUT));
endmodule

module decodeur (
  input  RCMP,
  input  CLK,
  input  [23:0] in_3,
  output WE,
  output [1:0] SlctType,
  output [2:0] SlctOP,
  output [1:0] Slct,
  output STOR,
  output JMP,
  output [3:0] RIn1,
  output [3:0] RIn2,
  output [7:0] ADDR8,
  output [3:0] Rout
);

  wire and_3_out, and_4_out, decodmemoire_1_jeq, decodmemoire_1_jmp, decodmemoire_1_jne, not_1_out, or_2_out;
  wire [1:1] deco_we_1_we;
  wire [3:0] reg_24bit_1_q_2;
  wire [23:0] multiplexer_1_out;
  wire [23:16] reg_24bit_1_q;

  Multiplexer #(.width(24)) multiplexer_1 (.in0(in_3), .in1({24{1'b0}}), .out(multiplexer_1_out), .sel(JMP));
  Reg_24Bit reg_24bit_1 (
    .CLK(CLK), .WE(1'b1), .D(multiplexer_1_out), .Q({reg_24bit_1_q, RIn1, RIn2, reg_24bit_1_q_2, Rout}));
  assign SlctType = {2{deco_we_1_we[1]}} & reg_24bit_1_q[20:19];  // AND_Gate and_1, 2 bits wide
  Deco_WE deco_we_1 (.in_1(reg_24bit_1_q), .WE(deco_we_1_we[1]));
  assign SlctOP = {3{deco_we_1_we[1]}} & reg_24bit_1_q[18:16];  // AND_Gate and_2, 3 bits wide
  or or_1 (WE, deco_we_1_we[1], Slct[0], Slct[1]);
  DecodMemoire decodmemoire_1 (
    .E(reg_24bit_1_q[21:16]), .Load(Slct[0]), .Stor(STOR), .Cnst(Slct[1]), .JMP(decodmemoire_1_jmp),
    .JNE(decodmemoire_1_jne), .JEQ(decodmemoire_1_jeq));
  or or_2 (or_2_out, decodmemoire_1_jmp, Slct[1], STOR, Slct[0], and_4_out, and_3_out);
  not not_1 (not_1_out, RCMP);
  Multiplexer #(.width(8)) multiplexer_2 (.in1({RIn2, reg_24bit_1_q_2}), .out(ADDR8), .sel(or_2_out));  // open: in0
  and and_3 (and_3_out, decodmemoire_1_jne, not_1_out);
  and and_4 (and_4_out, RCMP, decodmemoire_1_jeq);
  or or_3 (JMP, decodmemoire_1_jmp, and_3_out, and_4_out);
endmodule

module Deco_WE (
  input  [7:0] in_1,
  output WE
);

  wire equal_8bit_1_s, equal_8bit_2_s, equal_8bit_3_s, equal_8bit_4_s, equal_8bit_5_s, equal_8bit_6_s,
       equal_8bit_7_s, equal_8bit_8_s, equal_8bit_9_s, equal_8bit_10_s, equal_8bit_11_s, equal_8bit_12_s,
       equal_8bit_13_s, equal_8bit_14_s, equal_8bit_15_s, equal_8bit_16_s, equal_8bit_17_s, equal_8bit_18_s,
       equal_8bit_19_s, equal_8bit_20_s, equal_8bit_21_s, equal_8bit_22_s, equal_8bit_23_s, equal_8bit_24_s,
       equal_8bit_25_s, or_1_out;

  Equal_8Bit equal_8bit_1 (.A(in_1), .B(8'h18), .S(equal_8bit_1_s));
  Equal_8Bit equal_8bit_2 (.A(in_1), .B(8'h19), .S(equal_8bit_2_s));
  Equal_8Bit equal_8bit_3 (.A(in_1), .B(8'h10), .S(equal_8bit_3_s));
  Equal_8Bit equal_8bit_4 (.A(in_1), .B(8'h11), .S(equal_8bit_4_s));
  Equal_8Bit equal_8bit_5 (.A(in_1), .B(8'h12), .S(equal_8bit_5_s));
  Equal_8Bit equal_8bit_6 (.A(in_1), .B(8'h9), .S(equal_8bit_6_s));
  Equal_8Bit equal_8bit_7 (.A(in_1), .B(8'ha), .S(equal_8bit_7_s));
  Equal_8Bit equal_8bit_8 (.A(in_1), .B(8'hb), .S(equal_8bit_8_s));
  Equal_8Bit equal_8bit_9 (.A(in_1), .B(8'hc), .S(equal_8bit_9_s));
  Equal_8Bit equal_8bit_10 (.A(in_1), .B(8'h1), .S(equal_8bit_10_s));
  Equal_8Bit equal_8bit_11 (.A(in_1), .B(8'h3), .S(equal_8bit_11_s));
  Equal_8Bit equal_8bit_12 (.A(in_1), .B(8'h5), .S(equal_8bit_12_s));
  Equal_8Bit equal_8bit_13 (.A(in_1), .B(8'h6), .S(equal_8bit_13_s));
  or or_1 (or_1_out, equal_8bit_1_s, equal_8bit_2_s, equal_8bit_3_s, equal_8bit_4_s, equal_8bit_5_s, equal_8bit_6_s, equal_8bit_7_s, equal_8bit_8_s, equal_8bit_9_s, equal_8bit_10_s, equal_8bit_11_s, equal_8bit_12_s, equal_8bit_13_s);
  Equal_8Bit equal_8bit_14 (.A(in_1), .B(8'h1b), .S(equal_8bit_14_s));
  Equal_8Bit equal_8bit_15 (.A(in_1), .B(8'h1a), .S(equal_8bit_15_s));
  Equal_8Bit equal_8bit_16 (.A(in_1), .B(8'h1c), .S(equal_8bit_16_s));
  Equal_8Bit equal_8bit_17 (.A(in_1), .B(8'h1d), .S(equal_8bit_17_s));
  Equal_8Bit equal_8bit_18 (.A(in_1), .B(8'h1f), .S(equal_8bit_18_s));
  Equal_8Bit equal_8bit_19 (.A(in_1), .B(8'h1e), .S(equal_8bit_19_s));
  Equal_8Bit equal_8bit_20 (.A(in_1), .B(8'h13), .S(equal_8bit_20_s));
  Equal_8Bit equal_8bit_21 (.A(in_1), .B(8'h14), .S(equal_8bit_21_s));
  Equal_8Bit equal_8bit_22 (.A(in_1), .B(8'h15), .S(equal_8bit_22_s));
  Equal_8Bit equal_8bit_23 (.A(in_1), .B(8'h8), .S(equal_8bit_23_s));
  Equal_8Bit equal_8bit_24 (.A(in_1), .B(8'h2), .S(equal_8bit_24_s));
  Equal_8Bit equal_8bit_25 (.A(in_1), .B(8'h4), .S(equal_8bit_25_s));
  or or_2 (WE, equal_8bit_14_s, equal_8bit_15_s, equal_8bit_16_s, equal_8bit_17_s, equal_8bit_18_s, equal_8bit_19_s, or_1_out, equal_8bit_20_s, equal_8bit_21_s, equal_8bit_22_s, equal_8bit_23_s, equal_8bit_24_s, equal_8bit_25_s);
endmodule

module DecodMemoire (
  input  [5:0] E,
  output Load,
  output Stor,
  output Cnst,
  output JMP,
  output JNE,
  output JEQ
);

  wire and_1_out, decoder_1_out0, not_1_out;

  not not_1 (not_1_out, E[4]);
  and and_1 (and_1_out, not_1_out, E[5]);
  Decoder #(.select(3)) decoder_1 (
    .out0(decoder_1_out0), .out1(Load), .out2(Stor), .out3(decoder_1_out0), .out4(Cnst), .out5(JMP),
    .out6(JNE), .out7(JEQ), .sel(E[2:0]), .en(and_1_out));
  // NoConnect on decoder_1_out0
endmodule

module Reg_ALU (
  input  CLK,
  input  [7:0] RegIn,
  input  [3:0] SlctA,
  input  [3:0] SlctC,
  input  WE,
  input  [2:0] SlctOP,
  input  [3:0] SlctB,
  input  [1:0] SlctType,
  output [7:0] RegOut,
  output [7:0] ALUOut,
  output Er,
  output RCMP,
  output [7:0] PRINT_B,
  output [7:0] PRINT_A,
  output [63:0] PRINT_R
);

  wire [7:0] alu_1_s, bancreg_1_r9, bancreg_1_r10, bancreg_1_r11, bancreg_1_r12, bancreg_1_r13,
       bancreg_1_r14, bancreg_1_r15, bancreg_1_r16;

  BancReg bancreg_1 (
    .CLK(CLK), .C(RegIn), .SlctC(SlctC), .WE(WE), .R1(PRINT_R[63:56]), .R2(PRINT_R[55:48]),
    .R3(PRINT_R[47:40]), .R4(PRINT_R[39:32]), .R5(PRINT_R[31:24]), .R6(PRINT_R[23:16]), .R7(PRINT_R[15:8]),
    .R8(PRINT_R[7:0]), .R9(bancreg_1_r9), .R10(bancreg_1_r10), .R11(bancreg_1_r11), .R12(bancreg_1_r12),
    .R13(bancreg_1_r13), .R14(bancreg_1_r14), .R15(bancreg_1_r15), .R16(bancreg_1_r16), .RCMP(RCMP));
  Multiplexer #(.select(4), .width(8)) multiplexer_1 (
    .in0(PRINT_R[63:56]), .in1(PRINT_R[55:48]), .in2(PRINT_R[47:40]), .in3(PRINT_R[39:32]),
    .in4(PRINT_R[31:24]), .in5(PRINT_R[23:16]), .in6(PRINT_R[15:8]), .in7(PRINT_R[7:0]), .in8(bancreg_1_r9),
    .in9(bancreg_1_r10), .in10(bancreg_1_r11), .in11(bancreg_1_r12), .in12(bancreg_1_r13),
    .in13(bancreg_1_r14), .in14(bancreg_1_r15), .in15(bancreg_1_r16), .out(PRINT_A), .sel(SlctA));
  Multiplexer #(.select(4), .width(8)) multiplexer_2 (
    .in0(PRINT_R[63:56]), .in1(PRINT_R[55:48]), .in2(PRINT_R[47:40]), .in3(PRINT_R[39:32]),
    .in4(PRINT_R[31:24]), .in5(PRINT_R[23:16]), .in6(PRINT_R[15:8]), .in7(PRINT_R[7:0]), .in8(bancreg_1_r9),
    .in9(bancreg_1_r10), .in10(bancreg_1_r11), .in11(bancreg_1_r12), .in12(bancreg_1_r13),
    .in13(bancreg_1_r14), .in14(bancreg_1_r15), .in15(bancreg_1_r16), .out(PRINT_B), .sel(SlctB));
  ALU alu_1 (.A(PRINT_A), .B(PRINT_B), .SltcOP(SlctOP), .SltcType(SlctType), .S(alu_1_s), .Er(Er));
  assign ALUOut = alu_1_s & {8{WE}};  // AND_Gate and_1, 8 bits wide

  assign RegOut = PRINT_A;
endmodule

module BancReg (
  input  CLK,
  input  [7:0] C,
  input  [3:0] SlctC,
  input  WE,
  output [7:0] R1,
  output [7:0] R2,
  output [7:0] R3,
  output [7:0] R4,
  output [7:0] R5,
  output [7:0] R6,
  output [7:0] R7,
  output [7:0] R8,
  output [7:0] R9,
  output [7:0] R10,
  output [7:0] R11,
  output [7:0] R12,
  output [7:0] R13,
  output [7:0] R14,
  output [7:0] R15,
  output [7:0] R16,
  output RCMP
);

  wire decoder_1_out0, decoder_1_out1, decoder_1_out2, decoder_1_out3, decoder_1_out4, decoder_1_out5,
       decoder_1_out6, decoder_1_out7, decoder_1_out8, decoder_1_out9, decoder_1_out10, decoder_1_out11,
       decoder_1_out12, decoder_1_out13, decoder_1_out14, decoder_1_out15;

  Decoder #(.select(4)) decoder_1 (
    .out0(decoder_1_out0), .out1(decoder_1_out1), .out2(decoder_1_out2), .out3(decoder_1_out3),
    .out4(decoder_1_out4), .out5(decoder_1_out5), .out6(decoder_1_out6), .out7(decoder_1_out7),
    .out8(decoder_1_out8), .out9(decoder_1_out9), .out10(decoder_1_out10), .out11(decoder_1_out11),
    .out12(decoder_1_out12), .out13(decoder_1_out13), .out14(decoder_1_out14), .out15(decoder_1_out15),
    .sel(SlctC), .en(WE));
  // NoConnect on C[7:1]
  Reg_8Bit reg_8bit_1 (.D(C), .WE(decoder_1_out0), .CLK(CLK), .Q(R1));
  Reg_8Bit reg_8bit_2 (.D(C), .WE(decoder_1_out1), .CLK(CLK), .Q(R2));
  Reg_8Bit reg_8bit_3 (.D(C), .WE(decoder_1_out2), .CLK(CLK), .Q(R3));
  Reg_8Bit reg_8bit_4 (.D(C), .WE(decoder_1_out3), .CLK(CLK), .Q(R4));
  Reg_8Bit reg_8bit_5 (.D(C), .WE(decoder_1_out4), .CLK(CLK), .Q(R5));
  Reg_8Bit reg_8bit_6 (.D(C), .WE(decoder_1_out5), .CLK(CLK), .Q(R6));
  Reg_8Bit reg_8bit_7 (.D(C), .WE(decoder_1_out6), .CLK(CLK), .Q(R7));
  Reg_1Bit reg_1bit_1 (.D(C[0]), .WE(decoder_1_out7), .CLK(CLK), .Q(R8[0]));
  Reg_8Bit reg_8bit_8 (.D(C), .WE(decoder_1_out8), .CLK(CLK), .Q(R9));
  Reg_8Bit reg_8bit_9 (.D(C), .WE(decoder_1_out9), .CLK(CLK), .Q(R10));
  Reg_8Bit reg_8bit_10 (.D(C), .WE(decoder_1_out10), .CLK(CLK), .Q(R11));
  Reg_8Bit reg_8bit_11 (.D(C), .WE(decoder_1_out11), .CLK(CLK), .Q(R12));
  Reg_8Bit reg_8bit_12 (.D(C), .WE(decoder_1_out12), .CLK(CLK), .Q(R13));
  Reg_8Bit reg_8bit_13 (.D(C), .WE(decoder_1_out13), .CLK(CLK), .Q(R14));
  Reg_8Bit reg_8bit_14 (.D(C), .WE(decoder_1_out14), .CLK(CLK), .Q(R15));
  Reg_8Bit reg_8bit_15 (.D(C), .WE(decoder_1_out15), .CLK(CLK), .Q(R16));

  assign R8[7:1] = {7{1'b0}};
  assign RCMP = R8[0];
endmodule

module CptRebour (
  input  [7:0] E,
  output [3:0] S2,
  output [3:0] S1
);

  Sub_8Bit sub_8bit_1 (.A({8{1'b1}}), .B(E), .S({S1, S2}));  // open: Er
endmodule

module Reg_24Bit (
  input  CLK,
  input  WE,
  input  [23:0] D,
  output [23:0] Q
);

  Reg_8Bit reg_8bit_1 (.D(D[7:0]), .WE(WE), .CLK(CLK), .Q(Q[7:0]));
  Reg_8Bit reg_8bit_2 (.D(D[15:8]), .WE(WE), .CLK(CLK), .Q(Q[15:8]));
  Reg_8Bit reg_8bit_3 (.D(D[23:16]), .WE(WE), .CLK(CLK), .Q(Q[23:16]));
endmodule

module Reg_8Bit (
  input  [7:0] D,
  input  WE,
  input  CLK,
  output [7:0] Q
);

  wire d_ff_1_qn, d_ff_2_qn, d_ff_3_qn, d_ff_4_qn, d_ff_6_qn, d_ff_7_qn, d_ff_8_qn, multiplexer_1_out,
       multiplexer_2_out, multiplexer_3_out, multiplexer_4_out, multiplexer_5_out, multiplexer_6_out,
       multiplexer_7_out, multiplexer_8_out;

  Multiplexer multiplexer_1 (.in0(Q[0]), .in1(D[0]), .out(multiplexer_1_out), .sel(WE));
  Multiplexer multiplexer_2 (.in0(Q[1]), .in1(D[1]), .out(multiplexer_2_out), .sel(WE));
  Multiplexer multiplexer_3 (.in0(Q[2]), .in1(D[2]), .out(multiplexer_3_out), .sel(WE));
  Multiplexer multiplexer_4 (.in0(Q[3]), .in1(D[3]), .out(multiplexer_4_out), .sel(WE));
  Multiplexer multiplexer_5 (.in0(Q[4]), .in1(D[4]), .out(multiplexer_5_out), .sel(WE));
  Multiplexer multiplexer_6 (.in0(Q[5]), .in1(D[5]), .out(multiplexer_6_out), .sel(WE));
  Multiplexer multiplexer_7 (.in0(Q[6]), .in1(D[6]), .out(multiplexer_7_out), .sel(WE));
  Multiplexer multiplexer_8 (.in0(Q[7]), .in1(D[7]), .out(multiplexer_8_out), .sel(WE));
  D_Flip_Flop d_ff_1 (.D(multiplexer_1_out), .clk(CLK), .Q(Q[0]), .Qn(d_ff_1_qn));  // open: preset, reset
  D_Flip_Flop d_ff_2 (.D(multiplexer_2_out), .clk(CLK), .Q(Q[1]), .Qn(d_ff_2_qn));  // open: preset, reset
  D_Flip_Flop d_ff_3 (.D(multiplexer_3_out), .clk(CLK), .Q(Q[2]), .Qn(d_ff_3_qn));  // open: preset, reset
  D_Flip_Flop d_ff_4 (.D(multiplexer_4_out), .clk(CLK), .Q(Q[3]), .Qn(d_ff_4_qn));  // open: preset, reset
  D_Flip_Flop d_ff_5 (.D(multiplexer_5_out), .clk(CLK), .Q(Q[4]));  // open: Qn, preset, reset
  D_Flip_Flop d_ff_6 (.D(multiplexer_6_out), .clk(CLK), .Q(Q[5]), .Qn(d_ff_6_qn));  // open: preset, reset
  D_Flip_Flop d_ff_7 (.D(multiplexer_7_out), .clk(CLK), .Q(Q[6]), .Qn(d_ff_7_qn));  // open: preset, reset
  D_Flip_Flop d_ff_8 (.D(multiplexer_8_out), .clk(CLK), .Q(Q[7]), .Qn(d_ff_8_qn));  // open: preset, reset
  // NoConnect on d_ff_1_qn
  // NoConnect on d_ff_2_qn
  // NoConnect on d_ff_3_qn
  // NoConnect on d_ff_4_qn
  // NoConnect on nothing
  // NoConnect on d_ff_6_qn
  // NoConnect on d_ff_7_qn
  // NoConnect on d_ff_8_qn
endmodule

module Reg_1Bit (
  input  D,
  input  WE,
  input  CLK,
  output Q
);

  wire and_1_out, d_ff_1_qn;

  and and_1 (and_1_out, WE, CLK);
  D_Flip_Flop d_ff_1 (.D(D), .clk(and_1_out), .Q(Q), .Qn(d_ff_1_qn));  // open: preset, reset
  // NoConnect on d_ff_1_qn
endmodule

module ALU (
  input  [7:0] A,
  input  [7:0] B,
  input  [2:0] SltcOP,
  input  [1:0] SltcType,
  output [7:0] S,
  output Er
);

  wire bloc_op_ari_1_err;
  wire [7:0] bloc_op_ari_1_s, bloc_op_comp_1_s, bloc_op_log_1_s, bloc_op_rot_1_s;

  BLOC_OP_COMP bloc_op_comp_1 (.A(A), .SlctOP(SltcOP), .B(B), .S(bloc_op_comp_1_s));
  BLOC_OP_ROT bloc_op_rot_1 (.A(A), .SlctOP(SltcOP), .S(bloc_op_rot_1_s));
  BLOC_OP_LOG bloc_op_log_1 (.SlctOP(SltcOP), .A(A), .B(B), .S(bloc_op_log_1_s));
  BLOC_OP_ARI bloc_op_ari_1 (.SlctOP(SltcOP), .B(B), .A(A), .S(bloc_op_ari_1_s), .Err(bloc_op_ari_1_err));
  Multiplexer #(.select(2), .width(8)) multiplexer_1 (
    .in0(bloc_op_comp_1_s), .in1(bloc_op_rot_1_s), .in2(bloc_op_log_1_s), .in3(bloc_op_ari_1_s), .out(S),
    .sel(SltcType));
  Multiplexer #(.select(2)) multiplexer_2 (
    .in0(1'b0), .in1(1'b0), .in2(1'b0), .in3(bloc_op_ari_1_err), .out(Er), .sel(SltcType));
endmodule

module BLOC_OP_LOG (
  input  [2:0] SlctOP,
  input  [7:0] A,
  input  [7:0] B,
  output [7:0] S
);

  wire [7:0] and_8bit_1_s, nand_8bit_1_s, nor_8bit_1_s, or_8bit_1_s, xnor_8bit_1_s, xor_8bit_1_s;

  And_8Bit and_8bit_1 (.A(A), .B(B), .S(and_8bit_1_s));
  Or_8Bit or_8bit_1 (.A(A), .B(B), .S(or_8bit_1_s));
  Xor_8Bit xor_8bit_1 (.A(A), .B(B), .S(xor_8bit_1_s));
  Nand_8Bit nand_8bit_1 (.A(A), .B(B), .S(nand_8bit_1_s));
  Nor_8Bit nor_8bit_1 (.A(A), .B(B), .S(nor_8bit_1_s));
  Xnor_8Bit xnor_8bit_1 (.A(A), .B(B), .S(xnor_8bit_1_s));
  Multiplexer #(.select(3), .width(8)) multiplexer_1 (
    .in0(and_8bit_1_s), .in1(or_8bit_1_s), .in2(xor_8bit_1_s), .in3(nand_8bit_1_s), .in4(nor_8bit_1_s),
    .in5(xnor_8bit_1_s), .in6({8{1'b0}}), .in7({8{1'b0}}), .out(S), .sel(SlctOP));
endmodule

module BLOC_OP_COMP (
  input  [7:0] A,
  input  [2:0] SlctOP,
  input  [7:0] B,
  output [7:0] S
);

  wire diff_8bit_1_s, equal_8bit_1_s, inf_8bit_1_s, infeq_8bit_1_s, sup_8bit_1_s, supeq_8bit_1_s;

  Inf_8Bit inf_8bit_1 (.A(A), .B(B), .S(inf_8bit_1_s));
  InfEq_8Bit infeq_8bit_1 (.A(A), .B(B), .S(infeq_8bit_1_s));
  Equal_8Bit equal_8bit_1 (.A(A), .B(B), .S(equal_8bit_1_s));
  SupEq_8Bit supeq_8bit_1 (.A(A), .B(B), .S(supeq_8bit_1_s));
  Sup_8Bit sup_8bit_1 (.A(A), .B(B), .S(sup_8bit_1_s));
  Diff_8Bit diff_8bit_1 (.A(A), .B(B), .S(diff_8bit_1_s));
  Multiplexer #(.select(3)) multiplexer_1 (
    .in0(1'b0), .in1(inf_8bit_1_s), .in2(infeq_8bit_1_s), .in3(equal_8bit_1_s), .in4(supeq_8bit_1_s),
    .in5(sup_8bit_1_s), .in6(diff_8bit_1_s), .in7(1'b0), .out(S[0]), .sel(SlctOP));

  assign S[7:1] = {7{1'b0}};
endmodule

module BLOC_OP_ARI (
  input  [2:0] SlctOP,
  input  [7:0] B,
  input  [7:0] A,
  output [7:0] S,
  output Err
);

  wire add_8bit_1_er, dec_8bit_1_er, inc_8bit_1_er, sub_8bit_1_er;
  wire [7:0] abs_8bit_1_s, add_8bit_1_s, dec_8bit_1_s, inc_8bit_1_s, max_8bit_1_s, min_8bit_1_s,
       neg_8bit_1_s, sub_8bit_1_s;

  Add_8Bit add_8bit_1 (.A(A), .B(B), .S(add_8bit_1_s), .Er(add_8bit_1_er));
  Sub_8Bit sub_8bit_1 (.A(A), .B(B), .S(sub_8bit_1_s), .Er(sub_8bit_1_er));
  Min_8Bit min_8bit_1 (.A(A), .B(B), .S(min_8bit_1_s));
  Max_8Bit max_8bit_1 (.A(A), .B(B), .S(max_8bit_1_s));
  Inc_8Bit inc_8bit_1 (.A(A), .S(inc_8bit_1_s), .Er(inc_8bit_1_er));
  Dec_8Bit dec_8bit_1 (.A(A), .S(dec_8bit_1_s), .Er(dec_8bit_1_er));
  Neg_8Bit neg_8bit_1 (.A(A), .S(neg_8bit_1_s));
  Abs_8Bit abs_8bit_1 (.A(A), .S(abs_8bit_1_s));
  or or_1 (Err, sub_8bit_1_er, dec_8bit_1_er, inc_8bit_1_er, add_8bit_1_er);
  Multiplexer #(.select(3), .width(8)) multiplexer_1 (
    .in0(add_8bit_1_s), .in1(sub_8bit_1_s), .in2(min_8bit_1_s), .in3(max_8bit_1_s), .in4(inc_8bit_1_s),
    .in5(dec_8bit_1_s), .in6(neg_8bit_1_s), .in7(abs_8bit_1_s), .out(S), .sel(SlctOP));
endmodule

module BLOC_OP_ROT (
  input  [7:0] A,
  input  [2:0] SlctOP,
  output [7:0] S
);

  wire [7:0] asr_8bit_1_s, lsl_8bit_1_s, lsr_8bit_1_s, not_8bit_1_s, rol_8bit_1_s, ror_8bit_1_s;

  Not_8Bit not_8bit_1 (.A(A), .S(not_8bit_1_s));
  Lsl_8Bit lsl_8bit_1 (.A(A), .S(lsl_8bit_1_s));
  Lsr_8Bit lsr_8bit_1 (.A(A), .S(lsr_8bit_1_s));
  Asr_8Bit asr_8bit_1 (.A(A), .S(asr_8bit_1_s));
  Rol_8Bit rol_8bit_1 (.A(A), .S(rol_8bit_1_s));
  Ror_8Bit ror_8bit_1 (.A(A), .S(ror_8bit_1_s));
  Multiplexer #(.select(3), .width(8)) multiplexer_1 (
    .in0(not_8bit_1_s), .in1(lsl_8bit_1_s), .in2(lsr_8bit_1_s), .in3(asr_8bit_1_s), .in4(rol_8bit_1_s),
    .in5(ror_8bit_1_s), .in6({8{1'b0}}), .in7({8{1'b0}}), .out(S), .sel(SlctOP));
endmodule

module Equal_1Bit (
  input  A,
  input  B,
  output S
);

  wire and_1_out, and_2_out, not_1_out, not_2_out;

  and and_1 (and_1_out, A, B);
  not not_1 (not_1_out, A);
  and and_2 (and_2_out, not_1_out, not_2_out);
  not not_2 (not_2_out, B);
  or or_1 (S, and_1_out, and_2_out);
endmodule

module Diff_1Bit (
  input  A,
  input  B,
  output S
);

  wire and_1_out, and_2_out, not_1_out, not_2_out, or_1_out;

  and and_1 (and_1_out, A, B);
  not not_1 (not_1_out, A);
  and and_2 (and_2_out, not_1_out, not_2_out);
  not not_2 (not_2_out, B);
  or or_1 (or_1_out, and_1_out, and_2_out);
  not not_3 (S, or_1_out);
endmodule

module Inf_1Bit (
  input  A,
  input  B,
  output S
);

  wire not_1_out;

  not not_1 (not_1_out, A);
  and and_1 (S, not_1_out, B);
endmodule

module InfFull_1Bit (
  input  A,
  input  B,
  input  R_1,
  output S
);

  wire and_1_out, and_2_out, and_3_out, not_1_out;

  not not_1 (not_1_out, A);
  and and_1 (and_1_out, not_1_out, R_1);
  and and_2 (and_2_out, not_1_out, B);
  and and_3 (and_3_out, B, R_1);
  or or_1 (S, and_1_out, and_2_out, and_3_out);
endmodule

module Sup_1Bit (
  input  A,
  input  B,
  output S
);

  wire not_1_out;

  not not_1 (not_1_out, A);
  and and_1 (S, not_1_out, B);
endmodule

module SupFull_1Bit (
  input  A,
  input  B,
  input  R_1,
  output S
);

  wire and_1_out, and_2_out, and_3_out, not_1_out;

  not not_1 (not_1_out, B);
  and and_1 (and_1_out, A, R_1);
  and and_2 (and_2_out, A, not_1_out);
  and and_3 (and_3_out, not_1_out, R_1);
  or or_1 (S, and_1_out, and_2_out, and_3_out);
endmodule

module Equal_8Bit (
  input  [7:0] A,
  input  [7:0] B,
  output S
);

  wire equal_1bit_1_s, equal_1bit_2_s, equal_1bit_3_s, equal_1bit_4_s, equal_1bit_5_s, equal_1bit_6_s,
       equal_1bit_7_s, equal_1bit_8_s;

  Equal_1Bit equal_1bit_1 (.A(A[0]), .B(B[0]), .S(equal_1bit_1_s));
  Equal_1Bit equal_1bit_2 (.A(A[1]), .B(B[1]), .S(equal_1bit_2_s));
  Equal_1Bit equal_1bit_3 (.A(A[2]), .B(B[2]), .S(equal_1bit_3_s));
  Equal_1Bit equal_1bit_4 (.A(A[3]), .B(B[3]), .S(equal_1bit_4_s));
  Equal_1Bit equal_1bit_5 (.A(A[4]), .B(B[4]), .S(equal_1bit_5_s));
  Equal_1Bit equal_1bit_6 (.A(A[5]), .B(B[5]), .S(equal_1bit_6_s));
  Equal_1Bit equal_1bit_7 (.A(A[6]), .B(B[6]), .S(equal_1bit_7_s));
  Equal_1Bit equal_1bit_8 (.A(A[7]), .B(B[7]), .S(equal_1bit_8_s));
  and and_1 (S, equal_1bit_1_s, equal_1bit_2_s, equal_1bit_3_s, equal_1bit_4_s, equal_1bit_5_s, equal_1bit_6_s, equal_1bit_7_s, equal_1bit_8_s);
endmodule

module Diff_8Bit (
  input  [7:0] A,
  input  [7:0] B,
  output S
);

  wire diff_1bit_1_s, diff_1bit_2_s, diff_1bit_3_s, diff_1bit_4_s, diff_1bit_5_s, diff_1bit_6_s,
       diff_1bit_7_s, diff_1bit_8_s;

  Diff_1Bit diff_1bit_1 (.A(A[0]), .B(B[0]), .S(diff_1bit_1_s));
  Diff_1Bit diff_1bit_2 (.A(A[1]), .B(B[1]), .S(diff_1bit_2_s));
  Diff_1Bit diff_1bit_3 (.A(A[2]), .B(B[2]), .S(diff_1bit_3_s));
  Diff_1Bit diff_1bit_4 (.A(A[3]), .B(B[3]), .S(diff_1bit_4_s));
  Diff_1Bit diff_1bit_5 (.A(A[4]), .B(B[4]), .S(diff_1bit_5_s));
  Diff_1Bit diff_1bit_6 (.A(A[5]), .B(B[5]), .S(diff_1bit_6_s));
  Diff_1Bit diff_1bit_7 (.A(A[6]), .B(B[6]), .S(diff_1bit_7_s));
  Diff_1Bit diff_1bit_8 (.A(A[7]), .B(B[7]), .S(diff_1bit_8_s));
  or or_1 (S, diff_1bit_1_s, diff_1bit_2_s, diff_1bit_3_s, diff_1bit_4_s, diff_1bit_5_s, diff_1bit_6_s, diff_1bit_7_s, diff_1bit_8_s);
endmodule

module Inf_8Bit (
  input  [7:0] A,
  input  [7:0] B,
  output S
);

  wire inffull_1bit_1_s, inffull_1bit_2_s, inffull_1bit_3_s, inffull_1bit_4_s, inffull_1bit_5_s,
       inffull_1bit_6_s, inffull_1bit_7_s;

  InfFull_1Bit inffull_1bit_1 (.A(A[0]), .B(B[0]), .R_1(1'b0), .S(inffull_1bit_1_s));
  InfFull_1Bit inffull_1bit_2 (.A(A[1]), .B(B[1]), .R_1(inffull_1bit_1_s), .S(inffull_1bit_2_s));
  InfFull_1Bit inffull_1bit_3 (.A(A[2]), .B(B[2]), .R_1(inffull_1bit_2_s), .S(inffull_1bit_3_s));
  InfFull_1Bit inffull_1bit_4 (.A(A[3]), .B(B[3]), .R_1(inffull_1bit_3_s), .S(inffull_1bit_4_s));
  InfFull_1Bit inffull_1bit_5 (.A(A[4]), .B(B[4]), .R_1(inffull_1bit_4_s), .S(inffull_1bit_5_s));
  InfFull_1Bit inffull_1bit_6 (.A(A[5]), .B(B[5]), .R_1(inffull_1bit_5_s), .S(inffull_1bit_6_s));
  InfFull_1Bit inffull_1bit_7 (.A(A[6]), .B(B[6]), .R_1(inffull_1bit_6_s), .S(inffull_1bit_7_s));
  InfFull_1Bit inffull_1bit_8 (.A(A[7]), .B(B[7]), .R_1(inffull_1bit_7_s), .S(S));
endmodule

module InfEq_8Bit (
  input  [7:0] A,
  input  [7:0] B,
  output S
);

  wire equal_8bit_1_s, inf_8bit_1_s;

  Inf_8Bit inf_8bit_1 (.A(A), .B(B), .S(inf_8bit_1_s));
  Equal_8Bit equal_8bit_1 (.A(A), .B(B), .S(equal_8bit_1_s));
  or or_1 (S, inf_8bit_1_s, equal_8bit_1_s);
endmodule

module Sup_8Bit (
  input  [7:0] A,
  input  [7:0] B,
  output S
);

  wire supfull_1bit_1_s, supfull_1bit_2_s, supfull_1bit_3_s, supfull_1bit_4_s, supfull_1bit_5_s,
       supfull_1bit_6_s, supfull_1bit_7_s;

  SupFull_1Bit supfull_1bit_1 (.A(A[0]), .B(B[0]), .R_1(1'b0), .S(supfull_1bit_1_s));
  SupFull_1Bit supfull_1bit_2 (.A(A[1]), .B(B[1]), .R_1(supfull_1bit_1_s), .S(supfull_1bit_2_s));
  SupFull_1Bit supfull_1bit_3 (.A(A[2]), .B(B[2]), .R_1(supfull_1bit_2_s), .S(supfull_1bit_3_s));
  SupFull_1Bit supfull_1bit_4 (.A(A[3]), .B(B[3]), .R_1(supfull_1bit_3_s), .S(supfull_1bit_4_s));
  SupFull_1Bit supfull_1bit_5 (.A(A[4]), .B(B[4]), .R_1(supfull_1bit_4_s), .S(supfull_1bit_5_s));
  SupFull_1Bit supfull_1bit_6 (.A(A[5]), .B(B[5]), .R_1(supfull_1bit_5_s), .S(supfull_1bit_6_s));
  SupFull_1Bit supfull_1bit_7 (.A(A[6]), .B(B[6]), .R_1(supfull_1bit_6_s), .S(supfull_1bit_7_s));
  SupFull_1Bit supfull_1bit_8 (.A(A[7]), .B(B[7]), .R_1(supfull_1bit_7_s), .S(S));
endmodule

module SupEq_8Bit (
  input  [7:0] A,
  input  [7:0] B,
  output S
);

  wire equal_8bit_1_s, sup_8bit_1_s;

  Sup_8Bit sup_8bit_1 (.A(A), .B(B), .S(sup_8bit_1_s));
  Equal_8Bit equal_8bit_1 (.A(A), .B(B), .S(equal_8bit_1_s));
  or or_1 (S, sup_8bit_1_s, equal_8bit_1_s);
endmodule

module And_8Bit (
  input  [7:0] A,
  input  [7:0] B,
  output [7:0] S
);

  assign S = A & B;  // AND_Gate and_1, 8 bits wide
endmodule

module Or_8Bit (
  input  [7:0] A,
  input  [7:0] B,
  output [7:0] S
);

  assign S = A | B;  // OR_Gate or_1, 8 bits wide
endmodule

module Xor_8Bit (
  input  [7:0] A,
  input  [7:0] B,
  output [7:0] S
);

  assign S = A ^ B;  // XOR_Gate xor_1, 8 bits wide
endmodule

module Nand_8Bit (
  input  [7:0] A,
  input  [7:0] B,
  output [7:0] S
);

  wire [7:0] and_1_out;

  assign and_1_out = A & B;  // AND_Gate and_1, 8 bits wide
  assign S = ~and_1_out;  // NOT_Gate not_1, 8 bits wide
endmodule

module Nor_8Bit (
  input  [7:0] A,
  input  [7:0] B,
  output [7:0] S
);

  wire [7:0] or_1_out;

  assign or_1_out = A | B;  // OR_Gate or_1, 8 bits wide
  assign S = ~or_1_out;  // NOT_Gate not_1, 8 bits wide
endmodule

module Xnor_8Bit (
  input  [7:0] A,
  input  [7:0] B,
  output [7:0] S
);

  wire [7:0] xor_1_out;

  assign xor_1_out = A ^ B;  // XOR_Gate xor_1, 8 bits wide
  assign S = ~xor_1_out;  // NOT_Gate not_1, 8 bits wide
endmodule

module Not_8Bit (
  input  [7:0] A,
  output [7:0] S
);

  assign S = ~A;  // NOT_Gate not_1, 8 bits wide
endmodule

module Lsl_8Bit (
  input  [7:0] A,
  output [7:0] S
);

  // NoConnect on A[7]

  assign S = {A[6:0], 1'b0};
endmodule

module Lsr_8Bit (
  input  [7:0] A,
  output [7:0] S
);

  // NoConnect on A[0]

  assign S = {1'b0, A[7:1]};
endmodule

module Asr_8Bit (
  input  [7:0] A,
  output [7:0] S
);

  // NoConnect on A[0]

  assign S = {{2{A[7]}}, A[6:1]};
endmodule

module Rol_8Bit (
  input  [7:0] A,
  output [7:0] S
);


  assign S = {A[6:0], A[7]};
endmodule

module Ror_8Bit (
  input  [7:0] A,
  output [7:0] S
);


  assign S = {A[0], A[7:1]};
endmodule

module Add_1Bit (
  input  Re,
  input  A,
  input  B,
  output S,
  output Rs
);

  wire and_1_out, and_2_out, or_1_out, xor_1_out;

  xor xor_1 (xor_1_out, A, B);
  or or_1 (or_1_out, B, Re);
  xor xor_2 (S, xor_1_out, Re);
  and and_1 (and_1_out, or_1_out, A);
  or or_2 (Rs, and_1_out, and_2_out);
  and and_2 (and_2_out, B, Re);
endmodule

module Add_8Bit (
  input  [7:0] A,
  input  [7:0] B,
  output [7:0] S,
  output Er
);

  wire add_1bit_1_rs, add_1bit_2_rs, add_1bit_3_rs, add_1bit_4_rs, add_1bit_5_rs, add_1bit_6_rs,
       add_1bit_7_rs;

  Add_1Bit add_1bit_1 (.Re(1'b0), .A(A[0]), .B(B[0]), .S(S[0]), .Rs(add_1bit_1_rs));
  Add_1Bit add_1bit_2 (.Re(add_1bit_1_rs), .A(A[1]), .B(B[1]), .S(S[1]), .Rs(add_1bit_2_rs));
  Add_1Bit add_1bit_3 (.Re(add_1bit_2_rs), .A(A[2]), .B(B[2]), .S(S[2]), .Rs(add_1bit_3_rs));
  Add_1Bit add_1bit_4 (.Re(add_1bit_3_rs), .A(A[3]), .B(B[3]), .S(S[3]), .Rs(add_1bit_4_rs));
  Add_1Bit add_1bit_5 (.Re(add_1bit_4_rs), .A(A[4]), .B(B[4]), .S(S[4]), .Rs(add_1bit_5_rs));
  Add_1Bit add_1bit_6 (.Re(add_1bit_5_rs), .A(A[5]), .B(B[5]), .S(S[5]), .Rs(add_1bit_6_rs));
  Add_1Bit add_1bit_7 (.Re(add_1bit_6_rs), .A(A[6]), .B(B[6]), .S(S[6]), .Rs(add_1bit_7_rs));
  Add_1Bit add_1bit_8 (.Re(add_1bit_7_rs), .A(A[7]), .B(B[7]), .S(S[7]), .Rs(Er));
endmodule

module CC2_8Bit (
  input  [7:0] A,
  output [7:0] S,
  output Er
);

  wire add_8bit_1_er;
  wire [7:0] not_1_out;

  assign not_1_out = ~A;  // NOT_Gate not_1, 8 bits wide
  Add_8Bit add_8bit_1 (.A(not_1_out), .B(8'h1), .S(S), .Er(add_8bit_1_er));
  // NoConnect on add_8bit_1_er
  Equal_8Bit equal_8bit_1 (.A(A), .B(8'h80), .S(Er));
endmodule

module Sub_8Bit (
  input  [7:0] A,
  input  [7:0] B,
  output [7:0] S,
  output Er
);

  wire add_8bit_1_er, cc2_8bit_1_er;
  wire [7:0] cc2_8bit_1_s;

  CC2_8Bit cc2_8bit_1 (.A(B), .S(cc2_8bit_1_s), .Er(cc2_8bit_1_er));
  Add_8Bit add_8bit_1 (.A(A), .B(cc2_8bit_1_s), .S(S), .Er(add_8bit_1_er));
  or or_1 (Er, add_8bit_1_er, cc2_8bit_1_er);
endmodule

module Max_8Bit (
  input  [7:0] A,
  input  [7:0] B,
  output [7:0] S
);

  wire inf_8bit_1_s;

  Multiplexer #(.width(8)) multiplexer_1 (.in0(A), .in1(B), .out(S), .sel(inf_8bit_1_s));
  Inf_8Bit inf_8bit_1 (.A(A), .B(B), .S(inf_8bit_1_s));
endmodule

module Min_8Bit (
  input  [7:0] A,
  input  [7:0] B,
  output [7:0] S
);

  wire sup_8bit_1_s;

  Multiplexer #(.width(8)) multiplexer_1 (.in0(A), .in1(B), .out(S), .sel(sup_8bit_1_s));
  Sup_8Bit sup_8bit_1 (.A(A), .B(B), .S(sup_8bit_1_s));
endmodule

module Inc_8Bit (
  input  [7:0] A,
  output [7:0] S,
  output Er
);

  Add_8Bit add_8bit_1 (.A(A), .B(8'h1), .S(S), .Er(Er));
endmodule

module Dec_8Bit (
  input  [7:0] A,
  output [7:0] S,
  output Er
);

  Sub_8Bit sub_8bit_1 (.A(A), .B(8'h1), .S(S), .Er(Er));
endmodule

module Abs_8Bit (
  input  [7:0] A,
  output [7:0] S
);

  wire cc2_8bit_1_er;
  wire [7:0] cc2_8bit_1_s;

  Multiplexer #(.width(8)) multiplexer_1 (.in0(A), .in1(cc2_8bit_1_s), .out(S), .sel(A[7]));
  CC2_8Bit cc2_8bit_1 (.A(A), .S(cc2_8bit_1_s), .Er(cc2_8bit_1_er));
  // NoConnect on cc2_8bit_1_er
endmodule

module Neg_8Bit (
  input  [7:0] A,
  output [7:0] S
);

  wire cc2_8bit_1_er;
  wire [7:0] cc2_8bit_1_s;

  CC2_8Bit cc2_8bit_1 (.A(A), .S(cc2_8bit_1_s), .Er(cc2_8bit_1_er));
  // NoConnect on cc2_8bit_1_er
  Multiplexer #(.width(8)) multiplexer_1 (.in0(cc2_8bit_1_s), .in1(A), .out(S), .sel(A[7]));
endmodule

module Affichage_8bit (
  input  [7:0] Eg,
  input  [7:0] Eb,
  input  [7:0] Ed,
  output [3:0] S1,
  output [3:0] S2
);

  assign {S2, S1} = Eg | Eb | Ed;  // OR_Gate or_1, 8 bits wide
endmodule
