// Logisim project projet.circ as structural Verilog
module add1Bit (
  input  Re,
  input  A,
  input  B,
  output S,
  output Rs
);

  wire and_1_out, and_2_out, or_1_out, xor_1_out;

  xor xor_1 (xor_1_out, A, B);
  or or_1 (or_1_out, B, Re);
  xor xor_2 (S, xor_1_out, Re);
  and and_1 (and_1_out, or_1_out, A);
  or or_2 (Rs, and_1_out, and_2_out);
  and and_2 (and_2_out, B, Re);
endmodule

module ADD (
  input  [7:0] A,
  input  [7:0] B,
  output [7:0] S
);

  wire add1bit_1_rs, add1bit_2_rs, add1bit_3_rs, add1bit_4_rs, add1bit_5_rs, add1bit_6_rs, add1bit_7_rs;

  add1Bit add1bit_1 (.A(A[0]), .B(B[0]), .S(S[0]), .Rs(add1bit_1_rs));  // open: Re
  add1Bit add1bit_2 (.Re(add1bit_1_rs), .A(A[1]), .B(B[1]), .S(S[1]), .Rs(add1bit_2_rs));
  add1Bit add1bit_3 (.Re(add1bit_2_rs), .A(A[2]), .B(B[2]), .S(S[2]), .Rs(add1bit_3_rs));
  add1Bit add1bit_4 (.Re(add1bit_3_rs), .A(A[3]), .B(B[3]), .S(S[3]), .Rs(add1bit_4_rs));
  add1Bit add1bit_5 (.Re(add1bit_4_rs), .A(A[4]), .B(B[4]), .S(S[4]), .Rs(add1bit_5_rs));
  add1Bit add1bit_6 (.Re(add1bit_5_rs), .A(A[5]), .B(B[5]), .S(S[5]), .Rs(add1bit_6_rs));
  add1Bit add1bit_7 (.Re(add1bit_6_rs), .A(A[6]), .B(B[6]), .S(S[6]), .Rs(add1bit_7_rs));
  add1Bit add1bit_8 (.Re(add1bit_7_rs), .A(A[7]), .B(B[7]), .S(S[7]));  // open: Rs
endmodule

module SUB (
  input  [7:0] B,
  input  [7:0] A,
  output [7:0] R
);

  wire [7:0] add_1_s, not_1_out;

  assign not_1_out = ~B;  // NOT_Gate not_1, 8 bits wide
  ADD add_1 (.A(not_1_out), .B(8'h1), .S(add_1_s));
  ADD add_2 (.A(add_1_s), .B(A), .S(R));
endmodule
